// Logisim project ep1.circ as structural Verilog: 16 circuits, main circuit main
module main (
  input  a0,
  input  a1,
  input  a2,
  input  c2,
  input  c1,
  input  c0,
  input  a3,
  input  a4,
  input  a5,
  input  a6,
  input  a7,
  input  b0,
  input  b1,
  input  b2,
  input  b3,
  input  b4,
  input  b5,
  input  b6,
  input  b7,
  output r0,
  output r1,
  output r2,
  output r3,
  output r4,
  output r5,
  output r6,
  output r7,
  output overflow
);

  ULA ula_1 (
    .overflow(overflow), .a0(a0), .a1(a1), .a2(a2), .a3(a3), .a4(a4), .a5(a5), .a6(a6), .a7(a7), .b0(b0),
    .b1(b1), .b2(b2), .b3(b3), .b4(b4), .b5(b5), .b6(b6), .b7(b7), .s2(c2), .s1(c1), .s0(c0), .r0(r0),
    .r1(r1), .r2(r2), .r3(r3), .r4(r4), .r5(r5), .r6(r6), .r7(r7));
endmodule

module halfAdder (
  input  a,
  input  b,
  output S,
  output Cout
);

  and and_1 (Cout, b, a);
  xor xor_1 (S, a, b);
endmodule

module fullAdder (
  input  Cin,
  input  a,
  input  b,
  output S,
  output Cout
);

  wire halfadder_1_cout, halfadder_1_s, halfadder_2_cout;

  halfAdder halfadder_1 (.a(a), .b(b), .S(halfadder_1_s), .Cout(halfadder_1_cout));
  xor xor_1 (Cout, halfadder_1_cout, halfadder_2_cout);
  halfAdder halfadder_2 (.a(Cin), .b(halfadder_1_s), .S(S), .Cout(halfadder_2_cout));
endmodule

module adicao (
  input  [7:0] A,
  input  [7:0] B,
  output [7:0] A_B,
  output overflow
);

  wire fulladder_1_cout, fulladder_2_cout, fulladder_3_cout, fulladder_4_cout, fulladder_5_cout,
       fulladder_6_cout, fulladder_7_cout, halfadder_1_cout;

  halfAdder halfadder_1 (.a(A[0]), .b(B[0]), .S(A_B[0]), .Cout(halfadder_1_cout));
  fullAdder fulladder_1 (.a(A[1]), .b(B[1]), .S(A_B[1]), .Cin(halfadder_1_cout), .Cout(fulladder_1_cout));
  fullAdder fulladder_2 (.a(A[2]), .b(B[2]), .S(A_B[2]), .Cin(fulladder_1_cout), .Cout(fulladder_2_cout));
  fullAdder fulladder_3 (.a(A[3]), .b(B[3]), .S(A_B[3]), .Cin(fulladder_2_cout), .Cout(fulladder_3_cout));
  fullAdder fulladder_4 (.a(A[4]), .b(B[4]), .S(A_B[4]), .Cin(fulladder_3_cout), .Cout(fulladder_4_cout));
  fullAdder fulladder_5 (.a(A[5]), .b(B[5]), .S(A_B[5]), .Cin(fulladder_4_cout), .Cout(fulladder_5_cout));
  fullAdder fulladder_6 (.a(A[6]), .b(B[6]), .S(A_B[6]), .Cin(fulladder_5_cout), .Cout(fulladder_6_cout));
  fullAdder fulladder_7 (.a(A[7]), .b(B[7]), .S(A_B[7]), .Cin(fulladder_6_cout), .Cout(fulladder_7_cout));
  xor xor_1 (overflow, fulladder_6_cout, fulladder_7_cout);
endmodule

module comp2 (
  input  [7:0] A,
  output [7:0] minus_A
);

  wire adicao_1_overflow;
  wire [7:0] not_1_out;

  assign not_1_out = ~A;  // NOT_Gate not_1, 8 bits wide
  adicao adicao_1 (.A(not_1_out), .B(8'h1), .A_B(minus_A), .overflow(adicao_1_overflow));
  // also tied to GND on the sheet: adicao_1_overflow
endmodule

module subtracao (
  input  [7:0] A,
  input  [7:0] B,
  output [7:0] A_B,
  output overflow
);

  wire [7:0] comp2_1_minus_a;

  adicao adicao_1 (.A(A), .B(comp2_1_minus_a), .A_B(A_B), .overflow(overflow));
  comp2 comp2_1 (.A(B), .minus_A(comp2_1_minus_a));
endmodule

module shift_left_once (
  input  [7:0] A,
  output Overflow,
  output [7:0] A_2
);


  assign A_2 = {A[6:0], 1'b0};
  assign Overflow = A[6];
  // also tied to GND on the sheet: A[7]
endmodule

module A___b__one_bit_multiplier (
  input  [7:0] A,
  input  bi,
  output [7:0] A_bi
);

  and and_1 (A_bi[6], A[6], bi);
  and and_2 (A_bi[7], A[7], bi);
  and and_3 (A_bi[4], A[4], bi);
  and and_4 (A_bi[5], A[5], bi);
  and and_5 (A_bi[2], A[2], bi);
  and and_6 (A_bi[3], A[3], bi);
  and and_7 (A_bi[0], A[0], bi);
  and and_8 (A_bi[1], A[1], bi);
endmodule

module unsignedMultiplication (
  input  [7:0] A___0,
  input  [7:0] B___0,
  output [7:0] AB,
  output Overflow
);

  wire adicao_1_overflow, adicao_2_overflow, adicao_3_overflow, adicao_4_overflow, adicao_5_overflow,
       adicao_6_overflow, shift_left_once_1_overflow, shift_left_once_2_overflow, shift_left_once_3_overflow,
       shift_left_once_4_overflow, shift_left_once_5_overflow, shift_left_once_6_overflow,
       shift_left_once_7_overflow, shift_left_once_8_overflow, shift_left_once_9_overflow,
       shift_left_once_10_overflow, shift_left_once_11_overflow, shift_left_once_12_overflow,
       shift_left_once_13_overflow, shift_left_once_14_overflow, shift_left_once_15_overflow,
       shift_left_once_16_overflow, shift_left_once_17_overflow, shift_left_once_18_overflow,
       shift_left_once_19_overflow, shift_left_once_20_overflow, shift_left_once_21_overflow;
  wire [7:0] a_b_one_bit_multiplier_1_a_bi, a_b_one_bit_multiplier_2_a_bi, a_b_one_bit_multiplier_3_a_bi,
       a_b_one_bit_multiplier_4_a_bi, a_b_one_bit_multiplier_5_a_bi, a_b_one_bit_multiplier_6_a_bi,
       a_b_one_bit_multiplier_7_a_bi, adicao_1_a_b, adicao_2_a_b, adicao_3_a_b, adicao_4_a_b, adicao_5_a_b,
       shift_left_once_1_a_2, shift_left_once_2_a_2, shift_left_once_3_a_2, shift_left_once_4_a_2,
       shift_left_once_5_a_2, shift_left_once_6_a_2, shift_left_once_7_a_2, shift_left_once_8_a_2,
       shift_left_once_9_a_2, shift_left_once_10_a_2, shift_left_once_11_a_2, shift_left_once_12_a_2,
       shift_left_once_13_a_2, shift_left_once_14_a_2, shift_left_once_15_a_2, shift_left_once_16_a_2,
       shift_left_once_17_a_2, shift_left_once_18_a_2, shift_left_once_19_a_2, shift_left_once_20_a_2,
       shift_left_once_21_a_2;
  wire [7:7] adicao_6_a_b;

  or or_1 (Overflow, shift_left_once_1_overflow, shift_left_once_2_overflow, shift_left_once_3_overflow, shift_left_once_4_overflow, shift_left_once_5_overflow, shift_left_once_6_overflow, shift_left_once_7_overflow, shift_left_once_8_overflow, shift_left_once_9_overflow, shift_left_once_10_overflow, shift_left_once_11_overflow, shift_left_once_12_overflow, shift_left_once_13_overflow, shift_left_once_14_overflow, shift_left_once_15_overflow, shift_left_once_16_overflow, shift_left_once_17_overflow, shift_left_once_18_overflow, shift_left_once_19_overflow, shift_left_once_20_overflow, shift_left_once_21_overflow, adicao_3_overflow, adicao_2_overflow, adicao_1_overflow, adicao_5_overflow, adicao_4_overflow, adicao_6_overflow);
  A___b__one_bit_multiplier a_b_one_bit_multiplier_1 (.bi(B___0[0]), .A_bi(a_b_one_bit_multiplier_1_a_bi), .A(A___0));
  A___b__one_bit_multiplier a_b_one_bit_multiplier_2 (.bi(B___0[1]), .A_bi(a_b_one_bit_multiplier_2_a_bi), .A(A___0));
  shift_left_once shift_left_once_1 (
    .A(a_b_one_bit_multiplier_2_a_bi), .A_2(shift_left_once_1_a_2), .Overflow(shift_left_once_1_overflow));
  A___b__one_bit_multiplier a_b_one_bit_multiplier_3 (.bi(B___0[2]), .A_bi(a_b_one_bit_multiplier_3_a_bi), .A(A___0));
  shift_left_once shift_left_once_2 (
    .A(a_b_one_bit_multiplier_3_a_bi), .A_2(shift_left_once_2_a_2), .Overflow(shift_left_once_2_overflow));
  shift_left_once shift_left_once_3 (
    .A(shift_left_once_2_a_2), .A_2(shift_left_once_3_a_2), .Overflow(shift_left_once_3_overflow));
  A___b__one_bit_multiplier a_b_one_bit_multiplier_4 (.bi(B___0[3]), .A_bi(a_b_one_bit_multiplier_4_a_bi), .A(A___0));
  shift_left_once shift_left_once_4 (
    .A(a_b_one_bit_multiplier_4_a_bi), .A_2(shift_left_once_4_a_2), .Overflow(shift_left_once_4_overflow));
  shift_left_once shift_left_once_5 (
    .A(shift_left_once_4_a_2), .A_2(shift_left_once_5_a_2), .Overflow(shift_left_once_5_overflow));
  shift_left_once shift_left_once_6 (
    .A(shift_left_once_5_a_2), .A_2(shift_left_once_6_a_2), .Overflow(shift_left_once_6_overflow));
  A___b__one_bit_multiplier a_b_one_bit_multiplier_5 (.bi(B___0[4]), .A_bi(a_b_one_bit_multiplier_5_a_bi), .A(A___0));
  shift_left_once shift_left_once_7 (
    .A(a_b_one_bit_multiplier_5_a_bi), .A_2(shift_left_once_7_a_2), .Overflow(shift_left_once_7_overflow));
  shift_left_once shift_left_once_8 (
    .A(shift_left_once_7_a_2), .A_2(shift_left_once_8_a_2), .Overflow(shift_left_once_8_overflow));
  shift_left_once shift_left_once_9 (
    .A(shift_left_once_8_a_2), .A_2(shift_left_once_9_a_2), .Overflow(shift_left_once_9_overflow));
  shift_left_once shift_left_once_10 (
    .A(shift_left_once_9_a_2), .A_2(shift_left_once_10_a_2), .Overflow(shift_left_once_10_overflow));
  A___b__one_bit_multiplier a_b_one_bit_multiplier_6 (.bi(B___0[5]), .A_bi(a_b_one_bit_multiplier_6_a_bi), .A(A___0));
  shift_left_once shift_left_once_11 (
    .A(a_b_one_bit_multiplier_6_a_bi), .A_2(shift_left_once_11_a_2), .Overflow(shift_left_once_11_overflow));
  shift_left_once shift_left_once_12 (
    .A(shift_left_once_11_a_2), .A_2(shift_left_once_12_a_2), .Overflow(shift_left_once_12_overflow));
  shift_left_once shift_left_once_13 (
    .A(shift_left_once_12_a_2), .A_2(shift_left_once_13_a_2), .Overflow(shift_left_once_13_overflow));
  shift_left_once shift_left_once_14 (
    .A(shift_left_once_13_a_2), .A_2(shift_left_once_14_a_2), .Overflow(shift_left_once_14_overflow));
  shift_left_once shift_left_once_15 (
    .A(shift_left_once_14_a_2), .A_2(shift_left_once_15_a_2), .Overflow(shift_left_once_15_overflow));
  A___b__one_bit_multiplier a_b_one_bit_multiplier_7 (.bi(B___0[6]), .A_bi(a_b_one_bit_multiplier_7_a_bi), .A(A___0));
  shift_left_once shift_left_once_16 (
    .A(a_b_one_bit_multiplier_7_a_bi), .A_2(shift_left_once_16_a_2), .Overflow(shift_left_once_16_overflow));
  shift_left_once shift_left_once_17 (
    .A(shift_left_once_16_a_2), .A_2(shift_left_once_17_a_2), .Overflow(shift_left_once_17_overflow));
  shift_left_once shift_left_once_18 (
    .A(shift_left_once_17_a_2), .A_2(shift_left_once_18_a_2), .Overflow(shift_left_once_18_overflow));
  shift_left_once shift_left_once_19 (
    .A(shift_left_once_18_a_2), .A_2(shift_left_once_19_a_2), .Overflow(shift_left_once_19_overflow));
  shift_left_once shift_left_once_20 (
    .A(shift_left_once_19_a_2), .A_2(shift_left_once_20_a_2), .Overflow(shift_left_once_20_overflow));
  shift_left_once shift_left_once_21 (
    .A(shift_left_once_20_a_2), .A_2(shift_left_once_21_a_2), .Overflow(shift_left_once_21_overflow));
  adicao adicao_1 (
    .A(a_b_one_bit_multiplier_1_a_bi), .B(shift_left_once_1_a_2), .A_B(adicao_1_a_b),
    .overflow(adicao_1_overflow));
  adicao adicao_2 (
    .A(shift_left_once_3_a_2), .B(shift_left_once_6_a_2), .A_B(adicao_2_a_b), .overflow(adicao_2_overflow));
  adicao adicao_3 (
    .A(shift_left_once_10_a_2), .B(shift_left_once_15_a_2), .A_B(adicao_3_a_b), .overflow(adicao_3_overflow));
  adicao adicao_4 (.A(adicao_1_a_b), .B(adicao_2_a_b), .A_B(adicao_4_a_b), .overflow(adicao_4_overflow));
  adicao adicao_5 (.A(adicao_3_a_b), .B(shift_left_once_21_a_2), .A_B(adicao_5_a_b), .overflow(adicao_5_overflow));
  adicao adicao_6 (.A(adicao_4_a_b), .B(adicao_5_a_b), .A_B({adicao_6_a_b[7], AB[6:0]}), .overflow(adicao_6_overflow));

  assign AB[7] = 1'b0;
  // also tied to GND on the sheet: {adicao_6_a_b[7], B___0[7]}
endmodule

module multiplication (
  input  [7:0] A,
  input  [7:0] B,
  output Overflow,
  output [7:0] A_B
);

  wire [7:0] absolutevalue_1_a_2, absolutevalue_2_a_2, and_1_out, and_2_out, comp2_1_minus_a, not_1_out,
       unsignedmultiplication_1_ab;
  wire [7:7] xor_1_out;

  xor xor_1 (xor_1_out[7], A[7], B[7]);
  absoluteValue absolutevalue_1 (.A(A), .A_2(absolutevalue_1_a_2));
  absoluteValue absolutevalue_2 (.A(B), .A_2(absolutevalue_2_a_2));
  unsignedMultiplication unsignedmultiplication_1 (
    .B___0(absolutevalue_2_a_2), .AB(unsignedmultiplication_1_ab), .Overflow(Overflow),
    .A___0(absolutevalue_1_a_2));
  comp2 comp2_1 (.A(unsignedmultiplication_1_ab), .minus_A(comp2_1_minus_a));
  assign and_1_out = unsignedmultiplication_1_ab & not_1_out;  // AND_Gate and_1, 8 bits wide
  assign not_1_out = ~{8{xor_1_out[7]}};  // NOT_Gate not_1, 8 bits wide
  assign and_2_out = comp2_1_minus_a & {8{xor_1_out[7]}};  // AND_Gate and_2, 8 bits wide
  assign A_B = and_1_out | and_2_out;  // OR_Gate or_1, 8 bits wide
endmodule

module absoluteValue (
  input  [7:0] A,
  output [7:0] A_2
);

  wire and_1_out, and_2_out, and_3_out, and_4_out, and_5_out, and_6_out, and_7_out, and_8_out, and_9_out,
       and_10_out, and_11_out, and_12_out, and_13_out, and_14_out, and_15_out, and_16_out, not_1_out;
  wire [7:0] comp2_1_minus_a;

  comp2 comp2_1 (.A(A), .minus_A(comp2_1_minus_a));
  not not_1 (not_1_out, A[7]);
  and and_1 (and_1_out, A[7], comp2_1_minus_a[7]);
  and and_2 (and_2_out, A[7], not_1_out);
  and and_3 (and_3_out, A[7], comp2_1_minus_a[6]);
  and and_4 (and_4_out, A[6], not_1_out);
  and and_5 (and_5_out, A[7], comp2_1_minus_a[5]);
  and and_6 (and_6_out, A[5], not_1_out);
  and and_7 (and_7_out, A[7], comp2_1_minus_a[4]);
  and and_8 (and_8_out, A[4], not_1_out);
  and and_9 (and_9_out, A[7], comp2_1_minus_a[3]);
  and and_10 (and_10_out, A[3], not_1_out);
  and and_11 (and_11_out, A[7], comp2_1_minus_a[2]);
  and and_12 (and_12_out, A[2], not_1_out);
  and and_13 (and_13_out, A[7], comp2_1_minus_a[1]);
  and and_14 (and_14_out, A[1], not_1_out);
  and and_15 (and_15_out, A[7], comp2_1_minus_a[0]);
  and and_16 (and_16_out, A[0], not_1_out);
  xor xor_1 (A_2[7], and_1_out, and_2_out);
  xor xor_2 (A_2[6], and_3_out, and_4_out);
  xor xor_3 (A_2[5], and_5_out, and_6_out);
  xor xor_4 (A_2[4], and_7_out, and_8_out);
  xor xor_5 (A_2[3], and_9_out, and_10_out);
  xor xor_6 (A_2[2], and_11_out, and_12_out);
  xor xor_7 (A_2[1], and_13_out, and_14_out);
  xor xor_8 (A_2[0], and_15_out, and_16_out);
endmodule

module divisionsub (
  input  a0,
  input  a1,
  input  a2,
  input  a3,
  input  a4,
  input  a5,
  input  a6,
  input  a7,
  input  b0,
  input  b1,
  input  b2,
  input  b3,
  input  b4,
  input  b5,
  input  b6,
  input  b7,
  output s0,
  output s1,
  output s2,
  output s3,
  output s4,
  output s5,
  output s6,
  output FinalQuo
);

  wire adicao_1_overflow, and_1_out, and_2_out, and_3_out, and_4_out, and_5_out, and_6_out, and_7_out,
       and_8_out, and_9_out, and_10_out, and_11_out, and_12_out, and_13_out, and_14_out;
  wire [7:0] adicao_1_a_b, comp2_1_minus_a;

  comp2 comp2_1 (.A({b7, b6, b5, b4, b3, b2, b1, b0}), .minus_A(comp2_1_minus_a));
  adicao adicao_1 (
    .A({a7, a6, a5, a4, a3, a2, a1, a0}), .B(comp2_1_minus_a), .A_B(adicao_1_a_b),
    .overflow(adicao_1_overflow));
  not not_1 (FinalQuo, adicao_1_a_b[7]);
  and and_1 (and_1_out, adicao_1_a_b[0], FinalQuo);
  and and_2 (and_2_out, adicao_1_a_b[1], FinalQuo);
  and and_3 (and_3_out, adicao_1_a_b[2], FinalQuo);
  and and_4 (and_4_out, adicao_1_a_b[3], FinalQuo);
  and and_5 (and_5_out, adicao_1_a_b[4], FinalQuo);
  and and_6 (and_6_out, adicao_1_a_b[5], FinalQuo);
  and and_7 (and_7_out, adicao_1_a_b[6], FinalQuo);
  and and_8 (and_8_out, a0, adicao_1_a_b[7]);
  and and_9 (and_9_out, a1, adicao_1_a_b[7]);
  and and_10 (and_10_out, a2, adicao_1_a_b[7]);
  and and_11 (and_11_out, a3, adicao_1_a_b[7]);
  and and_12 (and_12_out, a4, adicao_1_a_b[7]);
  and and_13 (and_13_out, a5, adicao_1_a_b[7]);
  and and_14 (and_14_out, a6, adicao_1_a_b[7]);
  or or_1 (s0, and_1_out, and_8_out);
  or or_2 (s1, and_2_out, and_9_out);
  or or_3 (s2, and_3_out, and_10_out);
  or or_4 (s3, and_4_out, and_11_out);
  or or_5 (s4, and_5_out, and_12_out);
  or or_6 (s5, and_6_out, and_13_out);
  or or_7 (s6, and_7_out, and_14_out);
  // also tied to GND on the sheet: adicao_1_overflow
endmodule

module unsignedDivision (
  input  a0,
  input  a1,
  input  a2,
  input  a3,
  input  a4,
  input  a5,
  input  a6,
  input  a7,
  input  b0,
  input  b1,
  input  b2,
  input  b3,
  input  b4,
  input  b5,
  input  b6,
  input  b7,
  output s7,
  output s6,
  output s5,
  output s4,
  output s3,
  output s2,
  output s1,
  output s0,
  output r0,
  output r1,
  output r2,
  output r3,
  output r4,
  output r5,
  output r6
);

  wire divisionsub_1_s0, divisionsub_1_s1, divisionsub_1_s2, divisionsub_1_s3, divisionsub_1_s4,
       divisionsub_1_s5, divisionsub_1_s6, divisionsub_2_s0, divisionsub_2_s1, divisionsub_2_s2,
       divisionsub_2_s3, divisionsub_2_s4, divisionsub_2_s5, divisionsub_2_s6, divisionsub_3_s0,
       divisionsub_3_s1, divisionsub_3_s2, divisionsub_3_s3, divisionsub_3_s4, divisionsub_3_s5,
       divisionsub_3_s6, divisionsub_4_s0, divisionsub_4_s1, divisionsub_4_s2, divisionsub_4_s3,
       divisionsub_4_s4, divisionsub_4_s5, divisionsub_4_s6, divisionsub_5_s0, divisionsub_5_s1,
       divisionsub_5_s2, divisionsub_5_s3, divisionsub_5_s4, divisionsub_5_s5, divisionsub_5_s6,
       divisionsub_6_s0, divisionsub_6_s1, divisionsub_6_s2, divisionsub_6_s3, divisionsub_6_s4,
       divisionsub_6_s5, divisionsub_6_s6, divisionsub_7_s0, divisionsub_7_s1, divisionsub_7_s2,
       divisionsub_7_s3, divisionsub_7_s4, divisionsub_7_s5, divisionsub_7_s6;

  divisionsub divisionsub_1 (
    .a0(a7), .a1(1'b0), .a2(1'b0), .a3(1'b0), .a4(1'b0), .a5(1'b0), .a6(1'b0), .a7(1'b0), .b0(b0), .b1(b1),
    .b2(b2), .b3(b3), .b4(b4), .b5(b5), .b6(b6), .b7(b7), .s0(divisionsub_1_s0), .s1(divisionsub_1_s1),
    .s2(divisionsub_1_s2), .s3(divisionsub_1_s3), .s4(divisionsub_1_s4), .s5(divisionsub_1_s5),
    .s6(divisionsub_1_s6), .FinalQuo(s7));
  divisionsub divisionsub_2 (
    .a0(a6), .a1(divisionsub_1_s0), .a2(divisionsub_1_s1), .a3(divisionsub_1_s2), .a4(divisionsub_1_s3),
    .a5(divisionsub_1_s4), .a6(divisionsub_1_s5), .a7(divisionsub_1_s6), .b0(b0), .b1(b1), .b2(b2), .b3(b3),
    .b4(b4), .b5(b5), .b6(b6), .b7(b7), .s0(divisionsub_2_s0), .s1(divisionsub_2_s1), .s2(divisionsub_2_s2),
    .s3(divisionsub_2_s3), .s4(divisionsub_2_s4), .s5(divisionsub_2_s5), .s6(divisionsub_2_s6), .FinalQuo(s6));
  divisionsub divisionsub_3 (
    .a0(a5), .a1(divisionsub_2_s0), .a2(divisionsub_2_s1), .a3(divisionsub_2_s2), .a4(divisionsub_2_s3),
    .a5(divisionsub_2_s4), .a6(divisionsub_2_s5), .a7(divisionsub_2_s6), .b0(b0), .b1(b1), .b2(b2), .b3(b3),
    .b4(b4), .b5(b5), .b6(b6), .b7(b7), .s0(divisionsub_3_s0), .s1(divisionsub_3_s1), .s2(divisionsub_3_s2),
    .s3(divisionsub_3_s3), .s4(divisionsub_3_s4), .s5(divisionsub_3_s5), .s6(divisionsub_3_s6), .FinalQuo(s5));
  divisionsub divisionsub_4 (
    .a0(a4), .a1(divisionsub_3_s0), .a2(divisionsub_3_s1), .a3(divisionsub_3_s2), .a4(divisionsub_3_s3),
    .a5(divisionsub_3_s4), .a6(divisionsub_3_s5), .a7(divisionsub_3_s6), .b0(b0), .b1(b1), .b2(b2), .b3(b3),
    .b4(b4), .b5(b5), .b6(b6), .b7(b7), .s0(divisionsub_4_s0), .s1(divisionsub_4_s1), .s2(divisionsub_4_s2),
    .s3(divisionsub_4_s3), .s4(divisionsub_4_s4), .s5(divisionsub_4_s5), .s6(divisionsub_4_s6), .FinalQuo(s4));
  divisionsub divisionsub_5 (
    .a0(a3), .a1(divisionsub_4_s0), .a2(divisionsub_4_s1), .a3(divisionsub_4_s2), .a4(divisionsub_4_s3),
    .a5(divisionsub_4_s4), .a6(divisionsub_4_s5), .a7(divisionsub_4_s6), .b0(b0), .b1(b1), .b2(b2), .b3(b3),
    .b4(b4), .b5(b5), .b6(b6), .b7(b7), .s0(divisionsub_5_s0), .s1(divisionsub_5_s1), .s2(divisionsub_5_s2),
    .s3(divisionsub_5_s3), .s4(divisionsub_5_s4), .s5(divisionsub_5_s5), .s6(divisionsub_5_s6), .FinalQuo(s3));
  divisionsub divisionsub_6 (
    .a0(a2), .a1(divisionsub_5_s0), .a2(divisionsub_5_s1), .a3(divisionsub_5_s2), .a4(divisionsub_5_s3),
    .a5(divisionsub_5_s4), .a6(divisionsub_5_s5), .a7(divisionsub_5_s6), .b0(b0), .b1(b1), .b2(b2), .b3(b3),
    .b4(b4), .b5(b5), .b6(b6), .b7(b7), .s0(divisionsub_6_s0), .s1(divisionsub_6_s1), .s2(divisionsub_6_s2),
    .s3(divisionsub_6_s3), .s4(divisionsub_6_s4), .s5(divisionsub_6_s5), .s6(divisionsub_6_s6), .FinalQuo(s2));
  divisionsub divisionsub_7 (
    .a0(a1), .a1(divisionsub_6_s0), .a2(divisionsub_6_s1), .a3(divisionsub_6_s2), .a4(divisionsub_6_s3),
    .a5(divisionsub_6_s4), .a6(divisionsub_6_s5), .a7(divisionsub_6_s6), .b0(b0), .b1(b1), .b2(b2), .b3(b3),
    .b4(b4), .b5(b5), .b6(b6), .b7(b7), .s0(divisionsub_7_s0), .s1(divisionsub_7_s1), .s2(divisionsub_7_s2),
    .s3(divisionsub_7_s3), .s4(divisionsub_7_s4), .s5(divisionsub_7_s5), .s6(divisionsub_7_s6), .FinalQuo(s1));
  divisionsub divisionsub_8 (
    .a0(a0), .a1(divisionsub_7_s0), .a2(divisionsub_7_s1), .a3(divisionsub_7_s2), .a4(divisionsub_7_s3),
    .a5(divisionsub_7_s4), .a6(divisionsub_7_s5), .a7(divisionsub_7_s6), .b0(b0), .b1(b1), .b2(b2), .b3(b3),
    .b4(b4), .b5(b5), .b6(b6), .b7(b7), .s0(r0), .s1(r1), .s2(r2), .s3(r3), .s4(r4), .s5(r5), .s6(r6),
    .FinalQuo(s0));
endmodule

module division (
  input  [7:0] A,
  input  [7:0] B,
  output [7:0] A_B,
  output Overflow,
  output [7:0] A_B_2
);

  wire and_1_out, and_2_out, and_3_out, and_4_out, and_5_out, and_6_out, and_7_out, and_8_out, and_9_out,
       and_10_out, and_11_out, and_12_out, and_13_out, and_14_out, and_15_out, and_16_out, and_17_out,
       and_18_out, and_19_out, and_20_out, and_21_out, and_22_out, and_23_out, and_24_out, and_25_out,
       and_26_out, and_27_out, and_28_out, and_29_out, and_30_out, not_2_out, not_3_out, or_1_out;
  wire [6:0] unsigneddivision_1_r0;
  wire [7:0] absolutevalue_1_a_2, absolutevalue_2_a_2, comp2_1_minus_a, comp2_2_minus_a,
       unsigneddivision_1_s0;

  absoluteValue absolutevalue_1 (.A(A), .A_2(absolutevalue_1_a_2));
  absoluteValue absolutevalue_2 (.A(B), .A_2(absolutevalue_2_a_2));
  or or_1 (or_1_out, absolutevalue_2_a_2[0], absolutevalue_2_a_2[1], absolutevalue_2_a_2[2], absolutevalue_2_a_2[3], absolutevalue_2_a_2[4], absolutevalue_2_a_2[5], absolutevalue_2_a_2[6], absolutevalue_2_a_2[7]);
  not not_1 (Overflow, or_1_out);
  unsignedDivision unsigneddivision_1 (
    .a0(absolutevalue_1_a_2[0]), .a1(absolutevalue_1_a_2[1]), .a2(absolutevalue_1_a_2[2]),
    .a3(absolutevalue_1_a_2[3]), .a4(absolutevalue_1_a_2[4]), .a5(absolutevalue_1_a_2[5]),
    .a6(absolutevalue_1_a_2[6]), .a7(absolutevalue_1_a_2[7]), .b0(absolutevalue_2_a_2[0]),
    .b1(absolutevalue_2_a_2[1]), .b2(absolutevalue_2_a_2[2]), .b3(absolutevalue_2_a_2[3]),
    .b4(absolutevalue_2_a_2[4]), .b5(absolutevalue_2_a_2[5]), .b6(absolutevalue_2_a_2[6]),
    .b7(absolutevalue_2_a_2[7]), .s7(unsigneddivision_1_s0[7]), .s6(unsigneddivision_1_s0[6]),
    .s5(unsigneddivision_1_s0[5]), .s4(unsigneddivision_1_s0[4]), .s3(unsigneddivision_1_s0[3]),
    .s2(unsigneddivision_1_s0[2]), .s1(unsigneddivision_1_s0[1]), .s0(unsigneddivision_1_s0[0]),
    .r0(unsigneddivision_1_r0[0]), .r1(unsigneddivision_1_r0[1]), .r2(unsigneddivision_1_r0[2]),
    .r3(unsigneddivision_1_r0[3]), .r4(unsigneddivision_1_r0[4]), .r5(unsigneddivision_1_r0[5]),
    .r6(unsigneddivision_1_r0[6]));
  comp2 comp2_1 (.A(unsigneddivision_1_s0), .minus_A(comp2_1_minus_a));
  comp2 comp2_2 (.A({1'b0, unsigneddivision_1_r0}), .minus_A(comp2_2_minus_a));
  xor xor_1 (A_B[7], A[7], B[7]);
  not not_2 (not_2_out, A_B[7]);
  not not_3 (not_3_out, A[7]);
  and and_1 (and_1_out, not_2_out, unsigneddivision_1_s0[6]);
  or or_2 (A_B[6], and_1_out, and_2_out);
  and and_2 (and_2_out, comp2_1_minus_a[1], A_B[7]);
  and and_3 (and_3_out, not_2_out, unsigneddivision_1_s0[5]);
  or or_3 (A_B[5], and_3_out, and_4_out);
  and and_4 (and_4_out, comp2_1_minus_a[2], A_B[7]);
  and and_5 (and_5_out, not_2_out, unsigneddivision_1_s0[4]);
  or or_4 (A_B[4], and_5_out, and_6_out);
  and and_6 (and_6_out, comp2_1_minus_a[3], A_B[7]);
  and and_7 (and_7_out, not_2_out, unsigneddivision_1_s0[3]);
  or or_5 (A_B[3], and_7_out, and_8_out);
  and and_8 (and_8_out, comp2_1_minus_a[4], A_B[7]);
  and and_9 (and_9_out, not_2_out, unsigneddivision_1_s0[2]);
  or or_6 (A_B[2], and_9_out, and_10_out);
  and and_10 (and_10_out, comp2_1_minus_a[5], A_B[7]);
  and and_11 (and_11_out, not_2_out, unsigneddivision_1_s0[1]);
  or or_7 (A_B[1], and_11_out, and_12_out);
  and and_12 (and_12_out, comp2_1_minus_a[6], A_B[7]);
  and and_13 (and_13_out, not_2_out, unsigneddivision_1_s0[0]);
  or or_8 (A_B[0], and_13_out, and_14_out);
  and and_14 (and_14_out, comp2_1_minus_a[7], A_B[7]);
  and and_15 (and_15_out, comp2_2_minus_a[0], A[7]);
  and and_16 (and_16_out, unsigneddivision_1_r0[0], not_3_out);
  and and_17 (and_17_out, comp2_2_minus_a[1], A[7]);
  and and_18 (and_18_out, unsigneddivision_1_r0[1], not_3_out);
  and and_19 (and_19_out, comp2_2_minus_a[2], A[7]);
  and and_20 (and_20_out, unsigneddivision_1_r0[2], not_3_out);
  and and_21 (and_21_out, comp2_2_minus_a[3], A[7]);
  and and_22 (and_22_out, unsigneddivision_1_r0[3], not_3_out);
  and and_23 (and_23_out, comp2_2_minus_a[4], A[7]);
  and and_24 (and_24_out, unsigneddivision_1_r0[4], not_3_out);
  and and_25 (and_25_out, comp2_2_minus_a[5], A[7]);
  and and_26 (and_26_out, unsigneddivision_1_r0[5], not_3_out);
  and and_27 (and_27_out, comp2_2_minus_a[6], A[7]);
  and and_28 (and_28_out, unsigneddivision_1_r0[6], not_3_out);
  and and_29 (and_29_out, comp2_2_minus_a[7], A[7]);
  and and_30 (and_30_out, 1'b0, not_3_out);
  or or_9 (A_B_2[0], and_15_out, and_16_out);
  or or_10 (A_B_2[1], and_17_out, and_18_out);
  or or_11 (A_B_2[2], and_19_out, and_20_out);
  or or_12 (A_B_2[3], and_21_out, and_22_out);
  or or_13 (A_B_2[4], and_23_out, and_24_out);
  or or_14 (A_B_2[5], and_25_out, and_26_out);
  or or_15 (A_B_2[6], and_27_out, and_28_out);
  or or_16 (A_B_2[7], and_29_out, and_30_out);
endmodule

module mux (
  input  c0,
  input  c1,
  input  c2,
  input  add_i,
  input  subt_i,
  input  mult_i,
  input  quot_i,
  input  remn_i,
  output chosenOne
);

  wire and_1_out, and_2_out, and_3_out, and_4_out, and_5_out, and_6_out, and_7_out, and_8_out, not_1_out,
       not_2_out, not_3_out;

  not not_1 (not_1_out, c0);
  not not_2 (not_2_out, c1);
  not not_3 (not_3_out, c2);
  and and_1 (and_1_out, add_i, not_1_out, not_2_out, not_3_out);
  and and_2 (and_2_out, subt_i, not_1_out, not_2_out, c2);
  and and_3 (and_3_out, mult_i, not_1_out, c1, not_3_out);
  and and_4 (and_4_out, quot_i, not_1_out, c1, c2);
  and and_5 (and_5_out, remn_i, c0, not_2_out, not_3_out);
  and and_6 (and_6_out, 1'b1, c0, not_2_out, c2);
  and and_7 (and_7_out, 1'b1, c0, c1, not_3_out);
  and and_8 (and_8_out, 1'b1, c0, c1, c2);
  or or_1 (chosenOne, and_1_out, and_2_out, and_3_out, and_4_out, and_5_out, and_6_out, and_7_out, and_8_out);
endmodule

module ULA (
  input  a0,
  input  a1,
  input  s2,
  input  s1,
  input  s0,
  input  a2,
  input  a3,
  input  a4,
  input  a5,
  input  a6,
  input  a7,
  input  b0,
  input  b1,
  input  b2,
  input  b3,
  input  b4,
  input  b5,
  input  b6,
  input  b7,
  output overflow,
  output r0,
  output r1,
  output r2,
  output r3,
  output r4,
  output r5,
  output r6,
  output r7
);

  wire adicao_1_overflow, division_1_overflow, multiplication_1_overflow, subtracao_1_overflow;
  wire [7:0] adicao_1_a_b, division_1_a_b, division_1_a_b_2, multiplication_1_a_b, subtracao_1_a_b;

  adicao adicao_1 (
    .A({a7, a6, a5, a4, a3, a2, a1, a0}), .B({b7, b6, b5, b4, b3, b2, b1, b0}), .A_B(adicao_1_a_b),
    .overflow(adicao_1_overflow));
  subtracao subtracao_1 (
    .A({a7, a6, a5, a4, a3, a2, a1, a0}), .B({b7, b6, b5, b4, b3, b2, b1, b0}), .A_B(subtracao_1_a_b),
    .overflow(subtracao_1_overflow));
  multiplication multiplication_1 (
    .A({a7, a6, a5, a4, a3, a2, a1, a0}), .B({b7, b6, b5, b4, b3, b2, b1, b0}),
    .Overflow(multiplication_1_overflow), .A_B(multiplication_1_a_b));
  division division_1 (
    .A({a7, a6, a5, a4, a3, a2, a1, a0}), .B({b7, b6, b5, b4, b3, b2, b1, b0}), .A_B(division_1_a_b),
    .A_B_2(division_1_a_b_2), .Overflow(division_1_overflow));
  mux mux_1 (
    .add_i(adicao_1_overflow), .subt_i(subtracao_1_overflow), .mult_i(multiplication_1_overflow),
    .quot_i(division_1_overflow), .remn_i(division_1_overflow), .chosenOne(overflow), .c0(s2), .c1(s1),
    .c2(s0));
  mux mux_2 (
    .add_i(adicao_1_a_b[0]), .subt_i(subtracao_1_a_b[0]), .mult_i(multiplication_1_a_b[0]),
    .quot_i(division_1_a_b[0]), .remn_i(division_1_a_b_2[0]), .chosenOne(r0), .c0(s2), .c1(s1), .c2(s0));
  mux mux_3 (
    .add_i(adicao_1_a_b[1]), .subt_i(subtracao_1_a_b[1]), .mult_i(multiplication_1_a_b[1]),
    .quot_i(division_1_a_b[1]), .remn_i(division_1_a_b_2[1]), .chosenOne(r1), .c0(s2), .c1(s1), .c2(s0));
  mux mux_4 (
    .add_i(adicao_1_a_b[2]), .subt_i(subtracao_1_a_b[2]), .mult_i(multiplication_1_a_b[2]),
    .quot_i(division_1_a_b[2]), .remn_i(division_1_a_b_2[2]), .chosenOne(r2), .c0(s2), .c1(s1), .c2(s0));
  mux mux_5 (
    .add_i(adicao_1_a_b[3]), .subt_i(subtracao_1_a_b[3]), .mult_i(multiplication_1_a_b[3]),
    .quot_i(division_1_a_b[3]), .remn_i(division_1_a_b_2[3]), .chosenOne(r3), .c0(s2), .c1(s1), .c2(s0));
  mux mux_6 (
    .add_i(adicao_1_a_b[4]), .subt_i(subtracao_1_a_b[4]), .mult_i(multiplication_1_a_b[4]),
    .quot_i(division_1_a_b[4]), .remn_i(division_1_a_b_2[4]), .chosenOne(r4), .c0(s2), .c1(s1), .c2(s0));
  mux mux_7 (
    .add_i(adicao_1_a_b[5]), .subt_i(subtracao_1_a_b[5]), .mult_i(multiplication_1_a_b[5]),
    .quot_i(division_1_a_b[5]), .remn_i(division_1_a_b_2[5]), .chosenOne(r5), .c0(s2), .c1(s1), .c2(s0));
  mux mux_8 (
    .add_i(adicao_1_a_b[6]), .subt_i(subtracao_1_a_b[6]), .mult_i(multiplication_1_a_b[6]),
    .quot_i(division_1_a_b[6]), .remn_i(division_1_a_b_2[6]), .chosenOne(r6), .c0(s2), .c1(s1), .c2(s0));
  mux mux_9 (
    .add_i(adicao_1_a_b[7]), .subt_i(subtracao_1_a_b[7]), .mult_i(multiplication_1_a_b[7]),
    .quot_i(division_1_a_b[7]), .remn_i(division_1_a_b_2[7]), .chosenOne(r7), .c0(s2), .c1(s1), .c2(s0));
endmodule
