// Logisim project ep2.circ as structural Verilog: 7 circuits, main circuit main
module main (
);

  wire adder_1_out, C_plus_plus, CL, CONT, j_k_ff_1_q, JMP, LDA, not_1_out, or_1_out, or_2_out, register_1_q,
       STA, STP;
  wire [7:0] END, END_I, multiplexer_1_out;
  wire [15:0] DATA, IN, IR_q;

  Clock clock_1 (.out(CL));
  not not_1 (not_1_out, or_1_out);
  or or_1 (or_1_out, JMP, STP);
  Counter PC (.load(or_1_out), .D(END_I), .count(not_1_out), .Q(END), .clk(C_plus_plus));  // open: carry, clr
  J_K_Flip_Flop j_k_ff_1 (.J(STP), .clk(CL), .K(1'b0), .Q(j_k_ff_1_q));  // open: Qn, preset, en, reset
  Register #(.width(1)) register_1 (.D(adder_1_out), .Q(register_1_q), .clk(CL));  // open: en, clr
  Adder #(.width(1)) adder_1 (.a(register_1_q), .b(1'b1), .out(adder_1_out));  // open: cin, cout
  J_K_Flip_Flop j_k_ff_2 (.J(j_k_ff_1_q), .clk(CL), .K(1'b0), .Qn(CONT));  // open: Q, preset, en, reset
  and and_1 (C_plus_plus, adder_1_out, CONT);
  Multiplexer #(.width(8), .enable("false")) multiplexer_1 (
    .in0(END), .in1(END_I), .out(multiplexer_1_out), .sel(or_2_out));
  or or_2 (or_2_out, LDA, STA);
  RAM #(.dataWidth(16), .bus("separate")) ram_1 (
    .addr(multiplexer_1_out), .din(IN), .data(DATA), .str(STA), .clk(C_plus_plus), .clr(STP));  // open: sel, ld
  Register #(.width(16)) ACC (.D(DATA), .en(LDA), .Q(IN), .clk(CL));  // open: clr
  control control_1 (
    .Adress_Instruction(IR_q), .adress(END_I), .STA(STA), .LDA(LDA), .JMP(JMP), .STP(STP));  // open: NOP
  Register #(.width(16)) IR (.D(DATA), .Q(IR_q), .clk(CL));  // open: en, clr

  // Notes on the sheet:
  //   CLOCK
  //   PC - MEXENDO COM O
  //   ENDEREÇO APONTADO NA RAM
  //   PROTOCOLO PARA PARADA PÓS STOP
  //   FASE CONVERTER
  //   MEXENDO COM A RAM
  //   MEXENDO COM O ACC
  //   MEXENDO COM O IR E CTRL
endmodule

module control (
  input  [15:0] Adress_Instruction,
  output [7:0] adress,
  output NOP,
  output STA,
  output LDA,
  output JMP,
  output STP
);

  NOP nop_1 (.instruction(Adress_Instruction[15:8]), .NOP(NOP));
  STA sta_1 (.in_1(Adress_Instruction[15:8]), .STA(STA));
  LDA lda_1 (.in_1(Adress_Instruction[15:8]), .LDA(LDA));
  JMP jmp_1 (.in_1(Adress_Instruction[15:8]), .JMP(JMP));
  STP stp_1 (.in_1(Adress_Instruction[15:8]), .STP(STP));

  assign adress = Adress_Instruction[7:0];
endmodule

module NOP (
  input  [7:0] instruction,
  output NOP
);

  and and_1 (NOP, ~instruction[0], instruction[1], ~instruction[2], ~instruction[3], instruction[4], instruction[5], ~instruction[6], ~instruction[7]);  // AND_Gate
endmodule

module STA (
  input  [7:0] in_1,
  output STA
);

  and and_1 (STA, ~in_1[0], ~in_1[1], in_1[2], in_1[3], ~in_1[4], ~in_1[5], ~in_1[6], ~in_1[7]);  // AND_Gate
endmodule

module LDA (
  input  [7:0] in_1,
  output LDA
);

  and and_1 (LDA, in_1[0], in_1[1], ~in_1[2], in_1[3], ~in_1[4], ~in_1[5], ~in_1[6], ~in_1[7]);  // AND_Gate
endmodule

module JMP (
  input  [7:0] in_1,
  output JMP
);

  and and_1 (JMP, in_1[0], in_1[1], ~in_1[2], ~in_1[3], in_1[4], in_1[5], ~in_1[6], ~in_1[7]);  // AND_Gate
endmodule

module STP (
  input  [7:0] in_1,
  output STP
);

  and and_1 (STP, ~in_1[0], in_1[1], in_1[2], ~in_1[3], ~in_1[4], ~in_1[5], in_1[6], ~in_1[7]);  // AND_Gate
endmodule
