// Logisim project ep3.circ as structural Verilog: 41 circuits, main circuit main
module main (
  input  [15:0] Entrada,
  output [15:0] Saida
);

  wire ADD, adder_1_out, and_2_out, C_plus_plus, CL, CONT, DIV, INN, JMP, LDA, MUL, not_1_out, not_2_out,
       or_1_out, or_2_out, or_3_out, or_4_out, or_5_out, OW, PRN, register_1_q, REM, SEMI_STP, STA, STP, SUB,
       xor_1_out;
  wire [7:0] END, END_I, mux_8x1_1_out_4;
  wire [15:0] DATA, IN, IR_q, mux_16x1_1_out_4, mux_16x1_2_out_4, RESUL;

  Clock clock_1 (.out(CL));
  not not_1 (not_1_out, JMP);
  Counter PC (.load(JMP), .D(END_I), .count(not_1_out), .Q(END), .clk(C_plus_plus), .clr(STP));  // open: carry
  or or_1 (or_1_out, OW, STP);
  Register #(.width(1)) register_1 (.D(adder_1_out), .Q(register_1_q), .clk(CL));  // open: en, clr
  J_K_Flip_Flop j_k_ff_1 (.J(or_1_out), .clk(CL), .K(1'b0), .Q(SEMI_STP));  // open: Qn, preset, en, reset
  Adder #(.width(1)) adder_1 (.a(register_1_q), .b(1'b1), .out(adder_1_out));  // open: cin, cout
  J_K_Flip_Flop j_k_ff_2 (.J(SEMI_STP), .clk(CL), .K(1'b0), .Qn(CONT));  // open: Q, preset, en, reset
  and and_1 (C_plus_plus, adder_1_out, CONT);
  and and_2 (and_2_out, CONT, or_2_out);
  or or_2 (or_2_out, REM, DIV, MUL, SUB, ADD, LDA, PRN, or_3_out);
  MUX_8x1 mux_8x1_1 (.A(END), .B(END_I), .out_4(mux_8x1_1_out_4), .control(and_2_out));
  MUX_16x1 mux_16x1_1 (.A(IN), .B(Entrada), .out_4(mux_16x1_1_out_4), .Controle(INN));
  or or_3 (or_3_out, INN, STA);
  // Probe on Entrada
  not not_2 (not_2_out, xor_1_out);
  xor xor_1 (xor_1_out, ~SEMI_STP, CONT);  // XOR_Gate
  RAM #(.dataWidth(16), .bus("separate")) ram_1 (
    .addr(mux_8x1_1_out_4), .din(mux_16x1_1_out_4), .data(DATA), .str(or_3_out), .sel(not_2_out),
    .clk(C_plus_plus));  // open: ld, clr
  Register #(.width(16)) u_SAIDA (.D(DATA), .en(PRN), .Q(Saida), .clk(CL));  // open: clr
  // Probe on Saida
  Register #(.width(16)) IR (.D(DATA), .Q(IR_q), .clk(CL));  // open: en, clr
  MUX_16x1 mux_16x1_2 (.A(DATA), .B(RESUL), .out_4(mux_16x1_2_out_4), .Controle(or_5_out));
  or or_4 (or_4_out, or_5_out, LDA);
  or or_5 (or_5_out, REM, DIV, MUL, SUB, ADD);
  control control_1 (
    .Adress_Instruction(IR_q), .adress(END_I), .STA(STA), .LDA(LDA), .JMP(JMP), .ACC(IN), .ADD(ADD),
    .SUB(SUB), .MUL(MUL), .DIV(DIV), .REM(REM), .RESUL(RESUL), .RAM(DATA), .STP(STP), .OW(OW), .INN(INN),
    .PRN(PRN));  // open: NOP
  Register #(.width(16)) ACC (.D(mux_16x1_2_out_4), .en(or_4_out), .Q(IN), .clk(CL));  // open: clr

  // Other names for the same wires on the sheet: Ent[15:0] = Entrada

  // Notes on the sheet:
  //   CLOCK
  //   PC - MEXENDO COM O
  //   ENDEREÇO APONTADO NA RAM
  //   PROTOCOLO PARA PARADA PÓS STOP
  //   FASE CONVERTER
  //   MEXENDO COM A RAM
  //   In/Out
  //   MEXENDO COM O ACC
  //   MEXENDO COM O IR E CTRL E ULA
endmodule

module control (
  input  [15:0] Adress_Instruction,
  input  [15:0] RAM,
  input  [15:0] ACC,
  output [7:0] adress,
  output NOP,
  output STA,
  output LDA,
  output JMP,
  output STP,
  output [15:0] RESUL,
  output ADD,
  output OW,
  output SUB,
  output MUL,
  output DIV,
  output REM,
  output INN,
  output PRN
);

  wire jdz_0x35_1_jdz, jdz_condition_1_jdz___c, jeq_0x37_1_jeq, jeq_condition_1_jeq_c, jge_0x39_1_jge,
       jge_condition_1_jge_c, jgt_0x36_1_jgt, jgt_condition_1_jgt_c, jle_0x34_1_jle, jle_condition_1_jgt_c,
       jlt_0x38_1_jlt, jlt_condition_1_jlt_c, jmp_0x33_1_jmp;
  wire [2:0] mux_3x5_1_out_34;

  INN_0x1F inn_0x1f_1 (.in_1(Adress_Instruction[15:8]), .INN(INN));
  PRN_0x29 prn_0x29_1 (.in_1(Adress_Instruction[15:8]), .PRN(PRN));
  NOP_0x32 nop_0x32_1 (.instruction(Adress_Instruction[15:8]), .NOP(NOP));
  STA_0x0c sta_0x0c_1 (.in_1(Adress_Instruction[15:8]), .STA(STA));
  LDA_0x0b lda_0x0b_1 (.in_1(Adress_Instruction[15:8]), .LDA(LDA));
  JMP_0x33 jmp_0x33_1 (.in_1(Adress_Instruction[15:8]), .JMP(jmp_0x33_1_jmp));
  STP_0x46 stp_0x46_1 (.in_1(Adress_Instruction[15:8]), .STP(STP));
  JGE_0x39 jge_0x39_1 (.in_1(Adress_Instruction[15:8]), .JGE(jge_0x39_1_jge));
  JLT_0x38 jlt_0x38_1 (.in_1(Adress_Instruction[15:8]), .JLT(jlt_0x38_1_jlt));
  JEQ_0x37 jeq_0x37_1 (.in_1(Adress_Instruction[15:8]), .JEQ(jeq_0x37_1_jeq));
  JGT_0x36 jgt_0x36_1 (.in_1(Adress_Instruction[15:8]), .JGT(jgt_0x36_1_jgt));
  JDZ_0x35 jdz_0x35_1 (.in_1(Adress_Instruction[15:8]), .JDZ(jdz_0x35_1_jdz));
  JLE_0x34 jle_0x34_1 (.in_1(Adress_Instruction[15:8]), .JLE(jle_0x34_1_jle));
  ADD_0x15 add_0x15_1 (.in_1(Adress_Instruction[15:8]), .ADD(ADD));
  SUB_0x16 sub_0x16_1 (.in_1(Adress_Instruction[15:8]), .SUB(SUB));
  MUL_0x17 mul_0x17_1 (.in_1(Adress_Instruction[15:8]), .MUL(MUL));
  DIV_0x18 div_0x18_1 (.in_1(Adress_Instruction[15:8]), .DIV(DIV));
  REM_0x19 rem_0x19_1 (.in_1(Adress_Instruction[15:8]), .REM(REM));
  JGE___CONDITION jge_condition_1 (.ACC(ACC), .IN(jge_0x39_1_jge), .JGE_C(jge_condition_1_jge_c));
  JLT___CONDITION jlt_condition_1 (.ACC(ACC), .IN(jlt_0x38_1_jlt), .JLT_C(jlt_condition_1_jlt_c));
  JEQ___CONDITION jeq_condition_1 (.ACC(ACC), .IN(jeq_0x37_1_jeq), .JEQ_C(jeq_condition_1_jeq_c));
  JGT___CONDITION jgt_condition_1 (.ACC(ACC), .IN(jgt_0x36_1_jgt), .JGT_C(jgt_condition_1_jgt_c));
  JDZ___CONDITION jdz_condition_1 (.ACC(ACC), .IN(jdz_0x35_1_jdz), .JDZ___C(jdz_condition_1_jdz___c));
  JLE___CONDITION jle_condition_1 (.ACC(ACC), .IN(jle_0x34_1_jle), .JGT_C(jle_condition_1_jgt_c));
  MUX_3x5 mux_3x5_1 (
    .A(3'b111), .B(3'b000), .C(3'b001), .E(3'b010), .I(3'b011), .Q(3'b100), .out_34(mux_3x5_1_out_34),
    .in_33({REM, DIV, MUL, SUB, ADD}));  // open: D, F, G, H, J, K, L, M, N, O, P, R, S, T, U, V, W, X, Y, Z, AA, BB, CC, DD, EE, FF
  or or_1 (JMP, jmp_0x33_1_jmp, jge_condition_1_jge_c, jlt_condition_1_jlt_c, jeq_condition_1_jeq_c, jgt_condition_1_jgt_c, jdz_condition_1_jdz___c, jle_condition_1_jgt_c);
  ULA ula_1 (.A(ACC), .B(RAM), .R(RESUL), .CONTROLE(mux_3x5_1_out_34), .OF(OW));

  assign adress = Adress_Instruction[7:0];
endmodule

module ULA (
  input  [2:0] CONTROLE,
  input  [15:0] A,
  input  [15:0] B,
  output [15:0] R,
  output OF
);

  wire OF_DIV_REM, OF_MUL, OF_SUB, OF_SUM;
  wire [15:0] ADD, DIV, MUL, REM, SUB;

  Sum sum_1 (.A(A), .B(B), .A_B(ADD), .Overflow(OF_SUM));
  Substraction substraction_1 (.A(A), .B(B), .A_B(SUB), .Overflow(OF_SUB));
  Multiplication multiplication_1 (.A(A), .B(B), .A_B(MUL), .Overflow(OF_MUL));
  Division division_1 (.A(A), .B(B), .DIV_0_OF(OF_DIV_REM), .A_B(DIV), .A_B_2(REM));
  MUX_1x3 mux_1x3_1 (
    .A(OF_SUM), .B(OF_SUB), .C(OF_MUL), .D(OF_DIV_REM), .E(OF_DIV_REM), .F(1'b0), .G(1'b0), .H(1'b0),
    .out_10(OF), .control(CONTROLE));
  MUX_16x3 mux_16x3_1 (
    .A(ADD), .B(SUB), .C(MUL), .D(DIV), .E(REM), .F({16{1'b0}}), .G({16{1'b0}}), .H({16{1'b0}}), .out_10(R),
    .in_9(CONTROLE));

  // Other names for the same wires on the sheet: SELECT[2:0] = CONTROLE

  // Notes on the sheet:
  //   Soma
  //   Subtração
  //   Multiplicação
  //   Divisão / Resto de Divisão
  //   Selecionando operação
  //   Selecionando Overflow
endmodule

module NOP_0x32 (
  input  [7:0] instruction,
  output NOP
);

  and and_1 (NOP, ~instruction[0], instruction[1], ~instruction[2], ~instruction[3], instruction[4], instruction[5], ~instruction[6], ~instruction[7]);  // AND_Gate
endmodule

module STA_0x0c (
  input  [7:0] in_1,
  output STA
);

  and and_1 (STA, ~in_1[0], ~in_1[1], in_1[2], in_1[3], ~in_1[4], ~in_1[5], ~in_1[6], ~in_1[7]);  // AND_Gate
endmodule

module LDA_0x0b (
  input  [7:0] in_1,
  output LDA
);

  and and_1 (LDA, in_1[0], in_1[1], ~in_1[2], in_1[3], ~in_1[4], ~in_1[5], ~in_1[6], ~in_1[7]);  // AND_Gate
endmodule

module JMP_0x33 (
  input  [7:0] in_1,
  output JMP
);

  and and_1 (JMP, in_1[0], in_1[1], ~in_1[2], ~in_1[3], in_1[4], in_1[5], ~in_1[6], ~in_1[7]);  // AND_Gate
endmodule

module STP_0x46 (
  input  [7:0] in_1,
  output STP
);

  and and_1 (STP, ~in_1[0], in_1[1], in_1[2], ~in_1[3], ~in_1[4], ~in_1[5], in_1[6], ~in_1[7]);  // AND_Gate
endmodule

module JGE_0x39 (
  input  [7:0] in_1,
  output JGE
);

  and and_1 (JGE, in_1[0], ~in_1[1], ~in_1[2], in_1[3], in_1[4], in_1[5], ~in_1[6], ~in_1[7]);  // AND_Gate
endmodule

module JLT_0x38 (
  input  [7:0] in_1,
  output JLT
);

  and and_1 (JLT, ~in_1[0], ~in_1[1], ~in_1[2], in_1[3], in_1[4], in_1[5], ~in_1[6], ~in_1[7]);  // AND_Gate
endmodule

module JEQ_0x37 (
  input  [7:0] in_1,
  output JEQ
);

  and and_1 (JEQ, in_1[0], in_1[1], in_1[2], ~in_1[3], in_1[4], in_1[5], ~in_1[6], ~in_1[7]);  // AND_Gate
endmodule

module JGT_0x36 (
  input  [7:0] in_1,
  output JGT
);

  and and_1 (JGT, ~in_1[0], in_1[1], in_1[2], ~in_1[3], in_1[4], in_1[5], ~in_1[6], ~in_1[7]);  // AND_Gate
endmodule

module JDZ_0x35 (
  input  [7:0] in_1,
  output JDZ
);

  and and_1 (JDZ, in_1[0], ~in_1[1], in_1[2], ~in_1[3], in_1[4], in_1[5], ~in_1[6], ~in_1[7]);  // AND_Gate
endmodule

module JLE_0x34 (
  input  [7:0] in_1,
  output JLE
);

  and and_1 (JLE, ~in_1[0], ~in_1[1], in_1[2], ~in_1[3], in_1[4], in_1[5], ~in_1[6], ~in_1[7]);  // AND_Gate
endmodule

module ADD_0x15 (
  input  [7:0] in_1,
  output ADD
);

  and and_1 (ADD, in_1[0], ~in_1[1], in_1[2], ~in_1[3], in_1[4], ~in_1[5], ~in_1[6], ~in_1[7]);  // AND_Gate
endmodule

module SUB_0x16 (
  input  [7:0] in_1,
  output SUB
);

  and and_1 (SUB, ~in_1[0], in_1[1], in_1[2], ~in_1[3], in_1[4], ~in_1[5], ~in_1[6], ~in_1[7]);  // AND_Gate
endmodule

module MUL_0x17 (
  input  [7:0] in_1,
  output MUL
);

  and and_1 (MUL, in_1[0], in_1[1], in_1[2], ~in_1[3], in_1[4], ~in_1[5], ~in_1[6], ~in_1[7]);  // AND_Gate
endmodule

module DIV_0x18 (
  input  [7:0] in_1,
  output DIV
);

  and and_1 (DIV, ~in_1[0], ~in_1[1], ~in_1[2], in_1[3], in_1[4], ~in_1[5], ~in_1[6], ~in_1[7]);  // AND_Gate
endmodule

module REM_0x19 (
  input  [7:0] in_1,
  output REM
);

  and and_1 (REM, in_1[0], ~in_1[1], ~in_1[2], in_1[3], in_1[4], ~in_1[5], ~in_1[6], ~in_1[7]);  // AND_Gate
endmodule

module INN_0x1F (
  input  [7:0] in_1,
  output INN
);

  and and_1 (INN, in_1[0], in_1[1], in_1[2], in_1[3], in_1[4], ~in_1[5], ~in_1[6], ~in_1[7]);  // AND_Gate
endmodule

module PRN_0x29 (
  input  [7:0] in_1,
  output PRN
);

  and and_1 (PRN, in_1[0], ~in_1[1], ~in_1[2], in_1[3], ~in_1[4], in_1[5], ~in_1[6], ~in_1[7]);  // AND_Gate
endmodule

module JGE___CONDITION (
  input  [15:0] ACC,
  input  IN,
  output JGE_C
);

  and and_1 (JGE_C, ~ACC[15], IN);  // AND_Gate
endmodule

module JLT___CONDITION (
  input  [15:0] ACC,
  input  IN,
  output JLT_C
);

  and and_1 (JLT_C, ACC[15], IN);
endmodule

module JEQ___CONDITION (
  input  [15:0] ACC,
  input  IN,
  output JEQ_C
);

  and and_1 (JEQ_C, ~ACC[0], ~ACC[1], ~ACC[2], ~ACC[3], ~ACC[4], ~ACC[5], ~ACC[6], ~ACC[7], ~ACC[8], ~ACC[9], ~ACC[10], ~ACC[11], ~ACC[12], ~ACC[13], ~ACC[14], ~ACC[15], IN);  // AND_Gate
endmodule

module JGT___CONDITION (
  input  [15:0] ACC,
  input  IN,
  output JGT_C
);

  wire not_1_out, or_1_out;

  not not_1 (not_1_out, ACC[15]);
  or or_1 (or_1_out, ACC[0], ACC[1], ACC[2], ACC[3], ACC[4], ACC[5], ACC[6], ACC[7], ACC[8], ACC[9], ACC[10], ACC[11], ACC[12], ACC[13], ACC[14]);
  and and_1 (JGT_C, or_1_out, not_1_out, IN);
endmodule

module JDZ___CONDITION (
  input  [15:0] ACC,
  input  IN,
  output JDZ___C
);

  wire or_1_out;

  or or_1 (or_1_out, ACC[0], ACC[1], ACC[2], ACC[3], ACC[4], ACC[5], ACC[6], ACC[7], ACC[8], ACC[9], ACC[10], ACC[11], ACC[12], ACC[13], ACC[14], ACC[15]);
  and and_1 (JDZ___C, or_1_out, IN);
endmodule

module JLE___CONDITION (
  input  [15:0] ACC,
  input  IN,
  output JGT_C
);

  wire jeq_condition_1_jeq_c, jlt_condition_1_jlt_c;

  JLT___CONDITION jlt_condition_1 (.ACC(ACC), .IN(IN), .JLT_C(jlt_condition_1_jlt_c));
  JEQ___CONDITION jeq_condition_1 (.ACC(ACC), .IN(IN), .JEQ_C(jeq_condition_1_jeq_c));
  or or_1 (JGT_C, jlt_condition_1_jlt_c, jeq_condition_1_jeq_c);
endmodule

module Sum (
  input  [15:0] A,
  input  [15:0] B,
  output [15:0] A_B,
  output Overflow
);

  wire adder_1_cout, adder_2_cout, adder_3_cout, adder_4_cout, adder_5_cout, adder_6_cout, adder_7_cout,
       adder_8_cout, adder_9_cout, adder_10_cout, adder_11_cout, adder_12_cout, adder_13_cout, adder_14_cout,
       adder_15_cout, adder_16_cout;

  Adder #(.width(1)) adder_1 (.a(A[0]), .b(B[0]), .out(A_B[0]), .cout(adder_1_cout));  // open: cin
  Adder #(.width(1)) adder_2 (.a(A[1]), .b(B[1]), .out(A_B[1]), .cin(adder_1_cout), .cout(adder_2_cout));
  Adder #(.width(1)) adder_3 (.a(A[2]), .b(B[2]), .out(A_B[2]), .cin(adder_2_cout), .cout(adder_3_cout));
  Adder #(.width(1)) adder_4 (.a(A[3]), .b(B[3]), .out(A_B[3]), .cin(adder_3_cout), .cout(adder_4_cout));
  Adder #(.width(1)) adder_5 (.a(A[4]), .b(B[4]), .out(A_B[4]), .cin(adder_4_cout), .cout(adder_5_cout));
  Adder #(.width(1)) adder_6 (.a(A[5]), .b(B[5]), .out(A_B[5]), .cin(adder_5_cout), .cout(adder_6_cout));
  Adder #(.width(1)) adder_7 (.a(A[6]), .b(B[6]), .out(A_B[6]), .cin(adder_6_cout), .cout(adder_7_cout));
  Adder #(.width(1)) adder_8 (.a(A[7]), .b(B[7]), .out(A_B[7]), .cin(adder_7_cout), .cout(adder_8_cout));
  Adder #(.width(1)) adder_9 (.a(A[8]), .b(B[8]), .out(A_B[8]), .cin(adder_8_cout), .cout(adder_9_cout));
  Adder #(.width(1)) adder_10 (.a(A[9]), .b(B[9]), .out(A_B[9]), .cin(adder_9_cout), .cout(adder_10_cout));
  Adder #(.width(1)) adder_11 (.a(A[10]), .b(B[10]), .out(A_B[10]), .cin(adder_10_cout), .cout(adder_11_cout));
  Adder #(.width(1)) adder_12 (.a(A[11]), .b(B[11]), .out(A_B[11]), .cin(adder_11_cout), .cout(adder_12_cout));
  Adder #(.width(1)) adder_13 (.a(A[12]), .b(B[12]), .out(A_B[12]), .cin(adder_12_cout), .cout(adder_13_cout));
  Adder #(.width(1)) adder_14 (.a(A[13]), .b(B[13]), .out(A_B[13]), .cin(adder_13_cout), .cout(adder_14_cout));
  Adder #(.width(1)) adder_15 (.a(A[14]), .b(B[14]), .out(A_B[14]), .cin(adder_14_cout), .cout(adder_15_cout));
  Adder #(.width(1)) adder_16 (.a(A[15]), .b(B[15]), .out(A_B[15]), .cin(adder_15_cout), .cout(adder_16_cout));
  xor xor_1 (Overflow, adder_16_cout, adder_15_cout);
endmodule

module _2_Complement (
  input  [15:0] A,
  output [15:0] minus_A
);

  wire sum_1_overflow;
  wire [15:0] not_1_out;

  assign not_1_out = ~A;  // NOT_Gate not_1, 16 bits wide
  Sum sum_1 (.A(not_1_out), .B(16'h1), .A_B(minus_A), .Overflow(sum_1_overflow));
  // also tied to GND on the sheet: sum_1_overflow
endmodule

module Substraction (
  input  [15:0] A,
  input  [15:0] B,
  output [15:0] A_B,
  output Overflow
);

  wire [15:0] n2_complement_1_minus_a;

  _2_Complement u_2_complement_1 (.A(B), .minus_A(n2_complement_1_minus_a));
  Sum sum_1 (.A(A), .B(n2_complement_1_minus_a), .A_B(A_B), .Overflow(Overflow));
endmodule

module left_shift (
  input  [15:0] A,
  output Overflow,
  output [15:0] A_2
);


  assign A_2 = {A[14:0], 1'b0};
  assign Overflow = A[14];
  // also tied to GND on the sheet: A[15]
endmodule

module A_b (
  input  [15:0] A,
  input  b,
  output [15:0] A_b
);

  and and_1 (A_b[14], b, A[14]);
  and and_2 (A_b[13], b, A[13]);
  and and_3 (A_b[15], b, A[15]);
  and and_4 (A_b[12], b, A[12]);
  and and_5 (A_b[11], b, A[11]);
  and and_6 (A_b[10], b, A[10]);
  and and_7 (A_b[9], b, A[9]);
  and and_8 (A_b[8], b, A[8]);
  and and_9 (A_b[7], b, A[7]);
  and and_10 (A_b[5], b, A[5]);
  and and_11 (A_b[6], b, A[6]);
  and and_12 (A_b[3], b, A[3]);
  and and_13 (A_b[2], b, A[2]);
  and and_14 (A_b[4], b, A[4]);
  and and_15 (A_b[0], b, A[0]);
  and and_16 (A_b[1], b, A[1]);
endmodule

module unsignedMultiplication (
  input  [15:0] A___0,
  input  [15:0] B___0,
  output [15:0] R,
  output Overflow
);

  wire O1, O2, O3, O4, O5, O6, O7, O8, O9, O10, O11, O12, O13, O14, O15, O16, O17, O18, O19, O20, O21, O22,
       O23, O24, O25, O26, O27, O28, O29, O30, O31, O32, O33, O34, O35, O36, O37, O38, O39, O40, O41, O42,
       O43, O44, O45, O46, O47, O48, O49, O50, O51, O52, O53, O54, O55, O56, O57, O58, O59, O60, O61, O62,
       O63, O64, O65, O66, O67, O68, O69, O70, O71, O72, O73, O74, O75, O76, O77, O78, O79, O80, O81, O82,
       O83, O84, O85, O86, O87, O88, O89, O90, O91, O92, O93, O94, O95, O96, O97, O98, O99, O100, O101, O102,
       O103, O104, O105, O106, O107, O108, O109, O110, O111, O112, O113, O114, O115, O116, O117, O118, O119,
       or_2_out, or_3_out, or_4_out, or_5_out;
  wire [15:0] a_b_2_a_b, a_b_3_a_b, a_b_4_a_b, a_b_5_a_b, a_b_6_a_b, a_b_7_a_b, a_b_8_a_b, a_b_9_a_b,
       a_b_10_a_b, a_b_11_a_b, a_b_12_a_b, a_b_13_a_b, a_b_14_a_b, a_b_15_a_b, left_shift_2_a_2,
       left_shift_4_a_2, left_shift_5_a_2, left_shift_7_a_2, left_shift_8_a_2, left_shift_9_a_2,
       left_shift_11_a_2, left_shift_12_a_2, left_shift_13_a_2, left_shift_14_a_2, left_shift_16_a_2,
       left_shift_17_a_2, left_shift_18_a_2, left_shift_19_a_2, left_shift_20_a_2, left_shift_22_a_2,
       left_shift_23_a_2, left_shift_24_a_2, left_shift_25_a_2, left_shift_26_a_2, left_shift_27_a_2,
       left_shift_29_a_2, left_shift_30_a_2, left_shift_31_a_2, left_shift_32_a_2, left_shift_33_a_2,
       left_shift_34_a_2, left_shift_35_a_2, left_shift_37_a_2, left_shift_38_a_2, left_shift_39_a_2,
       left_shift_40_a_2, left_shift_41_a_2, left_shift_42_a_2, left_shift_43_a_2, left_shift_44_a_2,
       left_shift_46_a_2, left_shift_47_a_2, left_shift_48_a_2, left_shift_49_a_2, left_shift_50_a_2,
       left_shift_51_a_2, left_shift_52_a_2, left_shift_53_a_2, left_shift_54_a_2, left_shift_56_a_2,
       left_shift_57_a_2, left_shift_58_a_2, left_shift_59_a_2, left_shift_60_a_2, left_shift_61_a_2,
       left_shift_62_a_2, left_shift_63_a_2, left_shift_64_a_2, left_shift_65_a_2, left_shift_67_a_2,
       left_shift_68_a_2, left_shift_69_a_2, left_shift_70_a_2, left_shift_71_a_2, left_shift_72_a_2,
       left_shift_73_a_2, left_shift_74_a_2, left_shift_75_a_2, left_shift_76_a_2, left_shift_77_a_2,
       left_shift_79_a_2, left_shift_80_a_2, left_shift_81_a_2, left_shift_82_a_2, left_shift_83_a_2,
       left_shift_84_a_2, left_shift_85_a_2, left_shift_86_a_2, left_shift_87_a_2, left_shift_88_a_2,
       left_shift_89_a_2, left_shift_90_a_2, left_shift_92_a_2, left_shift_93_a_2, left_shift_94_a_2,
       left_shift_95_a_2, left_shift_96_a_2, left_shift_97_a_2, left_shift_98_a_2, left_shift_99_a_2,
       left_shift_100_a_2, left_shift_101_a_2, left_shift_102_a_2, left_shift_103_a_2, left_shift_104_a_2,
       S1, S2, S3, S4, S5, S6, S7, S8, S9, S10, S11, S12, S13, S14, S15, sum_1_a_b, sum_2_a_b, sum_3_a_b,
       sum_4_a_b, sum_5_a_b, sum_6_a_b, sum_7_a_b, sum_8_a_b, sum_9_a_b, sum_10_a_b, sum_11_a_b, sum_12_a_b,
       sum_13_a_b;

  A_b a_b_1 (.b(B___0[0]), .A(A___0), .A_b(S1));
  A_b a_b_2 (.b(B___0[1]), .A(A___0), .A_b(a_b_2_a_b));
  left_shift left_shift_1 (.A(a_b_2_a_b), .A_2(S2), .Overflow(O1));
  A_b a_b_3 (.b(B___0[2]), .A(A___0), .A_b(a_b_3_a_b));
  left_shift left_shift_2 (.A(a_b_3_a_b), .A_2(left_shift_2_a_2), .Overflow(O2));
  left_shift left_shift_3 (.A(left_shift_2_a_2), .A_2(S3), .Overflow(O3));
  A_b a_b_4 (.b(B___0[3]), .A(A___0), .A_b(a_b_4_a_b));
  left_shift left_shift_4 (.A(a_b_4_a_b), .A_2(left_shift_4_a_2), .Overflow(O4));
  left_shift left_shift_5 (.A(left_shift_4_a_2), .A_2(left_shift_5_a_2), .Overflow(O5));
  left_shift left_shift_6 (.A(left_shift_5_a_2), .A_2(S4), .Overflow(O6));
  A_b a_b_5 (.b(B___0[4]), .A(A___0), .A_b(a_b_5_a_b));
  left_shift left_shift_7 (.A(a_b_5_a_b), .A_2(left_shift_7_a_2), .Overflow(O7));
  left_shift left_shift_8 (.A(left_shift_7_a_2), .A_2(left_shift_8_a_2), .Overflow(O8));
  left_shift left_shift_9 (.A(left_shift_8_a_2), .A_2(left_shift_9_a_2), .Overflow(O9));
  left_shift left_shift_10 (.A(left_shift_9_a_2), .A_2(S5), .Overflow(O10));
  or or_1 (Overflow, or_5_out, O110, O111, O112, O113, O114, O115, O116, O117, O118, O119);
  Sum sum_1 (.A(S1), .B(S2), .A_B(sum_1_a_b), .Overflow(O106));
  Sum sum_2 (.A(sum_1_a_b), .B(sum_3_a_b), .A_B(sum_2_a_b), .Overflow(O114));
  Sum sum_3 (.A(S3), .B(S4), .A_B(sum_3_a_b), .Overflow(O107));
  Sum sum_4 (.A(S5), .B(S6), .A_B(sum_4_a_b), .Overflow(O108));
  Sum sum_5 (.A(S7), .B(S8), .A_B(sum_5_a_b), .Overflow(O109));
  Sum sum_6 (.A(S9), .B(S10), .A_B(sum_6_a_b), .Overflow(O110));
  Sum sum_7 (.A(S11), .B(S12), .A_B(sum_7_a_b), .Overflow(O111));
  Sum sum_8 (.A(S13), .B(S14), .A_B(sum_8_a_b), .Overflow(O112));
  or or_2 (or_2_out, O1, O2, O3, O4, O5, O6, O7, O8, O9, O10, O11, O12, O13, O14, O15, O16, O17, O18, O19, O20, O21, O22, O23, O24, O25, O26, O27, O28);
  or or_3 (or_3_out, or_2_out, O29, O30, O31, O32, O33, O34, O35, O36, O37, O38, O39, O40, O41, O42, O43, O44, O45, O46, O47, O48, O49, O50, O51, O52, O53, O54, O55);
  or or_4 (or_4_out, or_3_out, O56, O57, O58, O59, O60, O61, O62, O63, O64, O65, O66, O67, O68, O69, O70, O71, O72, O73, O74, O75, O76, O77, O78, O79, O80, O81, O82);
  or or_5 (or_5_out, or_4_out, O83, O84, O85, O86, O87, O88, O89, O90, O91, O92, O93, O94, O95, O96, O97, O98, O99, O100, O101, O102, O103, O104, O105, O106, O107, O108, O109);
  A_b a_b_6 (.b(B___0[5]), .A(A___0), .A_b(a_b_6_a_b));
  left_shift left_shift_11 (.A(a_b_6_a_b), .A_2(left_shift_11_a_2), .Overflow(O11));
  left_shift left_shift_12 (.A(left_shift_11_a_2), .A_2(left_shift_12_a_2), .Overflow(O12));
  left_shift left_shift_13 (.A(left_shift_12_a_2), .A_2(left_shift_13_a_2), .Overflow(O13));
  left_shift left_shift_14 (.A(left_shift_13_a_2), .A_2(left_shift_14_a_2), .Overflow(O14));
  left_shift left_shift_15 (.A(left_shift_14_a_2), .A_2(S6), .Overflow(O15));
  A_b a_b_7 (.b(B___0[6]), .A(A___0), .A_b(a_b_7_a_b));
  left_shift left_shift_16 (.A(a_b_7_a_b), .A_2(left_shift_16_a_2), .Overflow(O16));
  left_shift left_shift_17 (.A(left_shift_16_a_2), .A_2(left_shift_17_a_2), .Overflow(O17));
  left_shift left_shift_18 (.A(left_shift_17_a_2), .A_2(left_shift_18_a_2), .Overflow(O18));
  left_shift left_shift_19 (.A(left_shift_18_a_2), .A_2(left_shift_19_a_2), .Overflow(O19));
  left_shift left_shift_20 (.A(left_shift_19_a_2), .A_2(left_shift_20_a_2), .Overflow(O20));
  left_shift left_shift_21 (.A(left_shift_20_a_2), .A_2(S7), .Overflow(O21));
  Sum sum_9 (.A(sum_4_a_b), .B(sum_5_a_b), .A_B(sum_9_a_b), .Overflow(O115));
  Sum sum_10 (.A(sum_6_a_b), .B(sum_7_a_b), .A_B(sum_10_a_b), .Overflow(O116));
  Sum sum_11 (.A(sum_8_a_b), .B(S15), .A_B(sum_11_a_b), .Overflow(O117));
  A_b a_b_8 (.b(B___0[7]), .A(A___0), .A_b(a_b_8_a_b));
  left_shift left_shift_22 (.A(a_b_8_a_b), .A_2(left_shift_22_a_2), .Overflow(O22));
  left_shift left_shift_23 (.A(left_shift_22_a_2), .A_2(left_shift_23_a_2), .Overflow(O23));
  left_shift left_shift_24 (.A(left_shift_23_a_2), .A_2(left_shift_24_a_2), .Overflow(O24));
  left_shift left_shift_25 (.A(left_shift_24_a_2), .A_2(left_shift_25_a_2), .Overflow(O25));
  left_shift left_shift_26 (.A(left_shift_25_a_2), .A_2(left_shift_26_a_2), .Overflow(O26));
  left_shift left_shift_27 (.A(left_shift_26_a_2), .A_2(left_shift_27_a_2), .Overflow(O27));
  left_shift left_shift_28 (.A(left_shift_27_a_2), .A_2(S8), .Overflow(O28));
  Sum sum_12 (.A(sum_2_a_b), .B(sum_9_a_b), .A_B(sum_12_a_b), .Overflow(O118));
  Sum sum_13 (.A(sum_10_a_b), .B(sum_11_a_b), .A_B(sum_13_a_b), .Overflow(O119));
  Sum sum_14 (.A(sum_12_a_b), .B(sum_13_a_b), .A_B(R), .Overflow(O113));
  A_b a_b_9 (.b(B___0[8]), .A(A___0), .A_b(a_b_9_a_b));
  left_shift left_shift_29 (.A(a_b_9_a_b), .A_2(left_shift_29_a_2), .Overflow(O29));
  left_shift left_shift_30 (.A(left_shift_29_a_2), .A_2(left_shift_30_a_2), .Overflow(O30));
  left_shift left_shift_31 (.A(left_shift_30_a_2), .A_2(left_shift_31_a_2), .Overflow(O31));
  left_shift left_shift_32 (.A(left_shift_31_a_2), .A_2(left_shift_32_a_2), .Overflow(O32));
  left_shift left_shift_33 (.A(left_shift_32_a_2), .A_2(left_shift_33_a_2), .Overflow(O33));
  left_shift left_shift_34 (.A(left_shift_33_a_2), .A_2(left_shift_34_a_2), .Overflow(O34));
  left_shift left_shift_35 (.A(left_shift_34_a_2), .A_2(left_shift_35_a_2), .Overflow(O35));
  left_shift left_shift_36 (.A(left_shift_35_a_2), .A_2(S9), .Overflow(O36));
  A_b a_b_10 (.b(B___0[9]), .A(A___0), .A_b(a_b_10_a_b));
  left_shift left_shift_37 (.A(a_b_10_a_b), .A_2(left_shift_37_a_2), .Overflow(O37));
  left_shift left_shift_38 (.A(left_shift_37_a_2), .A_2(left_shift_38_a_2), .Overflow(O38));
  left_shift left_shift_39 (.A(left_shift_38_a_2), .A_2(left_shift_39_a_2), .Overflow(O39));
  left_shift left_shift_40 (.A(left_shift_39_a_2), .A_2(left_shift_40_a_2), .Overflow(O40));
  left_shift left_shift_41 (.A(left_shift_40_a_2), .A_2(left_shift_41_a_2), .Overflow(O41));
  left_shift left_shift_42 (.A(left_shift_41_a_2), .A_2(left_shift_42_a_2), .Overflow(O42));
  left_shift left_shift_43 (.A(left_shift_42_a_2), .A_2(left_shift_43_a_2), .Overflow(O43));
  left_shift left_shift_44 (.A(left_shift_43_a_2), .A_2(left_shift_44_a_2), .Overflow(O44));
  left_shift left_shift_45 (.A(left_shift_44_a_2), .A_2(S10), .Overflow(O45));
  A_b a_b_11 (.b(B___0[10]), .A(A___0), .A_b(a_b_11_a_b));
  left_shift left_shift_46 (.A(a_b_11_a_b), .A_2(left_shift_46_a_2), .Overflow(O46));
  left_shift left_shift_47 (.A(left_shift_46_a_2), .A_2(left_shift_47_a_2), .Overflow(O47));
  left_shift left_shift_48 (.A(left_shift_47_a_2), .A_2(left_shift_48_a_2), .Overflow(O48));
  left_shift left_shift_49 (.A(left_shift_48_a_2), .A_2(left_shift_49_a_2), .Overflow(O49));
  left_shift left_shift_50 (.A(left_shift_49_a_2), .A_2(left_shift_50_a_2), .Overflow(O50));
  left_shift left_shift_51 (.A(left_shift_50_a_2), .A_2(left_shift_51_a_2), .Overflow(O51));
  left_shift left_shift_52 (.A(left_shift_51_a_2), .A_2(left_shift_52_a_2), .Overflow(O52));
  left_shift left_shift_53 (.A(left_shift_52_a_2), .A_2(left_shift_53_a_2), .Overflow(O53));
  left_shift left_shift_54 (.A(left_shift_53_a_2), .A_2(left_shift_54_a_2), .Overflow(O54));
  left_shift left_shift_55 (.A(left_shift_54_a_2), .A_2(S11), .Overflow(O55));
  A_b a_b_12 (.b(B___0[11]), .A(A___0), .A_b(a_b_12_a_b));
  left_shift left_shift_56 (.A(a_b_12_a_b), .A_2(left_shift_56_a_2), .Overflow(O56));
  left_shift left_shift_57 (.A(left_shift_56_a_2), .A_2(left_shift_57_a_2), .Overflow(O57));
  left_shift left_shift_58 (.A(left_shift_57_a_2), .A_2(left_shift_58_a_2), .Overflow(O58));
  left_shift left_shift_59 (.A(left_shift_58_a_2), .A_2(left_shift_59_a_2), .Overflow(O59));
  left_shift left_shift_60 (.A(left_shift_59_a_2), .A_2(left_shift_60_a_2), .Overflow(O60));
  left_shift left_shift_61 (.A(left_shift_60_a_2), .A_2(left_shift_61_a_2), .Overflow(O61));
  left_shift left_shift_62 (.A(left_shift_61_a_2), .A_2(left_shift_62_a_2), .Overflow(O62));
  left_shift left_shift_63 (.A(left_shift_62_a_2), .A_2(left_shift_63_a_2), .Overflow(O63));
  left_shift left_shift_64 (.A(left_shift_63_a_2), .A_2(left_shift_64_a_2), .Overflow(O64));
  left_shift left_shift_65 (.A(left_shift_64_a_2), .A_2(left_shift_65_a_2), .Overflow(O65));
  left_shift left_shift_66 (.A(left_shift_65_a_2), .A_2(S12), .Overflow(O66));
  A_b a_b_13 (.b(B___0[12]), .A(A___0), .A_b(a_b_13_a_b));
  left_shift left_shift_67 (.A(a_b_13_a_b), .A_2(left_shift_67_a_2), .Overflow(O67));
  left_shift left_shift_68 (.A(left_shift_67_a_2), .A_2(left_shift_68_a_2), .Overflow(O68));
  left_shift left_shift_69 (.A(left_shift_68_a_2), .A_2(left_shift_69_a_2), .Overflow(O69));
  left_shift left_shift_70 (.A(left_shift_69_a_2), .A_2(left_shift_70_a_2), .Overflow(O70));
  left_shift left_shift_71 (.A(left_shift_70_a_2), .A_2(left_shift_71_a_2), .Overflow(O71));
  left_shift left_shift_72 (.A(left_shift_71_a_2), .A_2(left_shift_72_a_2), .Overflow(O72));
  left_shift left_shift_73 (.A(left_shift_72_a_2), .A_2(left_shift_73_a_2), .Overflow(O73));
  left_shift left_shift_74 (.A(left_shift_73_a_2), .A_2(left_shift_74_a_2), .Overflow(O74));
  left_shift left_shift_75 (.A(left_shift_74_a_2), .A_2(left_shift_75_a_2), .Overflow(O75));
  left_shift left_shift_76 (.A(left_shift_75_a_2), .A_2(left_shift_76_a_2), .Overflow(O76));
  left_shift left_shift_77 (.A(left_shift_76_a_2), .A_2(left_shift_77_a_2), .Overflow(O77));
  left_shift left_shift_78 (.A(left_shift_77_a_2), .A_2(S13), .Overflow(O78));
  A_b a_b_14 (.b(B___0[13]), .A(A___0), .A_b(a_b_14_a_b));
  left_shift left_shift_79 (.A(a_b_14_a_b), .A_2(left_shift_79_a_2), .Overflow(O79));
  left_shift left_shift_80 (.A(left_shift_79_a_2), .A_2(left_shift_80_a_2), .Overflow(O80));
  left_shift left_shift_81 (.A(left_shift_80_a_2), .A_2(left_shift_81_a_2), .Overflow(O81));
  left_shift left_shift_82 (.A(left_shift_81_a_2), .A_2(left_shift_82_a_2), .Overflow(O82));
  left_shift left_shift_83 (.A(left_shift_82_a_2), .A_2(left_shift_83_a_2), .Overflow(O83));
  left_shift left_shift_84 (.A(left_shift_83_a_2), .A_2(left_shift_84_a_2), .Overflow(O84));
  left_shift left_shift_85 (.A(left_shift_84_a_2), .A_2(left_shift_85_a_2), .Overflow(O85));
  left_shift left_shift_86 (.A(left_shift_85_a_2), .A_2(left_shift_86_a_2), .Overflow(O86));
  left_shift left_shift_87 (.A(left_shift_86_a_2), .A_2(left_shift_87_a_2), .Overflow(O87));
  left_shift left_shift_88 (.A(left_shift_87_a_2), .A_2(left_shift_88_a_2), .Overflow(O88));
  left_shift left_shift_89 (.A(left_shift_88_a_2), .A_2(left_shift_89_a_2), .Overflow(O89));
  left_shift left_shift_90 (.A(left_shift_89_a_2), .A_2(left_shift_90_a_2), .Overflow(O90));
  left_shift left_shift_91 (.A(left_shift_90_a_2), .A_2(S14), .Overflow(O91));
  A_b a_b_15 (.b(B___0[14]), .A(A___0), .A_b(a_b_15_a_b));
  left_shift left_shift_92 (.A(a_b_15_a_b), .A_2(left_shift_92_a_2), .Overflow(O92));
  left_shift left_shift_93 (.A(left_shift_92_a_2), .A_2(left_shift_93_a_2), .Overflow(O93));
  left_shift left_shift_94 (.A(left_shift_93_a_2), .A_2(left_shift_94_a_2), .Overflow(O94));
  left_shift left_shift_95 (.A(left_shift_94_a_2), .A_2(left_shift_95_a_2), .Overflow(O95));
  left_shift left_shift_96 (.A(left_shift_95_a_2), .A_2(left_shift_96_a_2), .Overflow(O96));
  left_shift left_shift_97 (.A(left_shift_96_a_2), .A_2(left_shift_97_a_2), .Overflow(O97));
  left_shift left_shift_98 (.A(left_shift_97_a_2), .A_2(left_shift_98_a_2), .Overflow(O98));
  left_shift left_shift_99 (.A(left_shift_98_a_2), .A_2(left_shift_99_a_2), .Overflow(O99));
  left_shift left_shift_100 (.A(left_shift_99_a_2), .A_2(left_shift_100_a_2), .Overflow(O100));
  left_shift left_shift_101 (.A(left_shift_100_a_2), .A_2(left_shift_101_a_2), .Overflow(O101));
  left_shift left_shift_102 (.A(left_shift_101_a_2), .A_2(left_shift_102_a_2), .Overflow(O102));
  left_shift left_shift_103 (.A(left_shift_102_a_2), .A_2(left_shift_103_a_2), .Overflow(O103));
  left_shift left_shift_104 (.A(left_shift_103_a_2), .A_2(left_shift_104_a_2), .Overflow(O104));
  left_shift left_shift_105 (.A(left_shift_104_a_2), .A_2(S15), .Overflow(O105));

  // Other names for the same wires on the sheet: A[15:0] = A___0; b0 = B___0[0]; b1 = B___0[1]; b2 = B___0[2];
  //   b3 = B___0[3]; b4 = B___0[4]; b5 = B___0[5]; b6 = B___0[6]; b7 = B___0[7]; b8 = B___0[8]; b9 = B___0[9];
  //   b10 = B___0[10]; b11 = B___0[11]; b12 = B___0[12]; b13 = B___0[13]; b14 = B___0[14]; b15 = B___0[15];
  //   OF = Overflow; Result[15:0] = R
endmodule

module Multiplication (
  input  [15:0] A,
  input  [15:0] B,
  output [15:0] A_B,
  output Overflow
);

  wire [15:0] absolute_value_1_x, absolute_value_2_x, and_1_out, and_2_out, n2_complement_1_minus_a,
       unsignedmultiplication_1_r;
  wire [15:15] xor_1_out;

  // Probe on B
  // Probe on A
  Absolute_Value absolute_value_1 (.A(A), .X(absolute_value_1_x));
  Absolute_Value absolute_value_2 (.A(B), .X(absolute_value_2_x));
  xor xor_1 (xor_1_out[15], A[15], B[15]);
  unsignedMultiplication unsignedmultiplication_1 (
    .A___0(absolute_value_1_x), .B___0(absolute_value_2_x), .R(unsignedmultiplication_1_r),
    .Overflow(Overflow));
  _2_Complement u_2_complement_1 (.A(unsignedmultiplication_1_r), .minus_A(n2_complement_1_minus_a));
  assign and_1_out = unsignedmultiplication_1_r & ~{16{xor_1_out[15]}};  // AND_Gate and_1, 16 bits wide
  assign and_2_out = n2_complement_1_minus_a & {16{xor_1_out[15]}};  // AND_Gate and_2, 16 bits wide
  assign A_B = and_1_out | and_2_out;  // OR_Gate or_1, 16 bits wide
  // Probe on A_B
endmodule

module Absolute_Value (
  input  [15:0] A,
  output [15:0] X
);

  wire [15:0] and_1_out, and_2_out, minus_A;

  _2_Complement u_2_complement_1 (.A(A), .minus_A(minus_A));
  assign and_1_out = A & ~{16{A[15]}};  // AND_Gate and_1, 16 bits wide
  assign and_2_out = minus_A & {16{A[15]}};  // AND_Gate and_2, 16 bits wide
  assign X = and_1_out ^ and_2_out;  // XOR_Gate xor_1, 16 bits wide

  // Other names for the same wires on the sheet: sgn = A[15]; SIGNAL[15:0] = {16{A[15]}}
endmodule

module Division (
  input  [15:0] A,
  input  [15:0] B,
  output DIV_0_OF,
  output [15:0] A_B,
  output [15:0] A_B_2
);

  wire AnswerSign;
  wire [14:0] Q, R;
  wire [15:0] absolute_value_1_x, absolute_value_2_x, and_2_out, and_3_out, and_4_out, and_5_out, minus_Q,
       minus_R;

  // Probe on A
  // Probe on B
  Absolute_Value absolute_value_1 (.A(A), .X(absolute_value_1_x));
  Absolute_Value absolute_value_2 (.A(B), .X(absolute_value_2_x));
  and and_1 (DIV_0_OF, ~B[0], ~B[1], ~B[2], ~B[3], ~B[4], ~B[5], ~B[6], ~B[7], ~B[8], ~B[9], ~B[10], ~B[11], ~B[12], ~B[13], ~B[14], ~B[15]);  // AND_Gate
  Divider #(.width(15)) divider_1 (
    .a(absolute_value_1_x[14:0]), .b(absolute_value_2_x[14:0]), .out(Q), .rem(R));  // open: upper
  _2_Complement u_2_complement_1 (.A({1'b0, R}), .minus_A(minus_R));
  xor xor_1 (AnswerSign, A[15], B[15]);
  assign and_2_out = {1'b0, Q} & ~{16{AnswerSign}};  // AND_Gate and_2, 16 bits wide
  assign and_3_out = minus_Q & {16{AnswerSign}};  // AND_Gate and_3, 16 bits wide
  _2_Complement u_2_complement_2 (.A({1'b0, Q}), .minus_A(minus_Q));
  assign A_B = and_2_out ^ and_3_out;  // XOR_Gate xor_2, 16 bits wide
  // Probe on {1'b0, R}
  // Probe on A_B
  assign and_4_out = {1'b0, R} & ~{16{A[15]}};  // AND_Gate and_4, 16 bits wide
  assign and_5_out = minus_R & {16{A[15]}};  // AND_Gate and_5, 16 bits wide
  assign A_B_2 = and_4_out ^ and_5_out;  // XOR_Gate xor_3, 16 bits wide
  // Probe on A_B_2

  // Other names for the same wires on the sheet: Sign_B = B[15]; Quocient[14:0] = Q; Remainder[14:0] = R;
  //   SIGNAL[15:0] = {16{AnswerSign}}; Sign_A = A[15]; Signal_A[15:0] = {16{A[15]}}
endmodule

module MUX_16x1 (
  input  [15:0] A,
  input  [15:0] B,
  input  Controle,
  output [15:0] out_4
);

  wire and_1_out, and_2_out, and_3_out, and_4_out, and_5_out, and_6_out, and_7_out, and_8_out, and_9_out,
       and_10_out, and_11_out, and_12_out, and_13_out, and_14_out, and_15_out, and_16_out, and_17_out,
       and_18_out, and_19_out, and_20_out, and_21_out, and_22_out, and_23_out, and_24_out, and_25_out,
       and_26_out, and_27_out, and_28_out, and_29_out, and_30_out, and_31_out, and_32_out;

  and and_1 (and_1_out, A[0], ~Controle);  // AND_Gate
  and and_2 (and_2_out, B[0], Controle);
  and and_3 (and_3_out, A[1], ~Controle);  // AND_Gate
  and and_4 (and_4_out, B[1], Controle);
  and and_5 (and_5_out, A[2], ~Controle);  // AND_Gate
  and and_6 (and_6_out, B[2], Controle);
  and and_7 (and_7_out, A[3], ~Controle);  // AND_Gate
  and and_8 (and_8_out, B[3], Controle);
  and and_9 (and_9_out, A[4], ~Controle);  // AND_Gate
  and and_10 (and_10_out, B[4], Controle);
  and and_11 (and_11_out, A[5], ~Controle);  // AND_Gate
  and and_12 (and_12_out, B[5], Controle);
  and and_13 (and_13_out, A[6], ~Controle);  // AND_Gate
  and and_14 (and_14_out, B[6], Controle);
  and and_15 (and_15_out, A[7], ~Controle);  // AND_Gate
  and and_16 (and_16_out, B[7], Controle);
  xor xor_1 (out_4[0], and_1_out, and_2_out);
  xor xor_2 (out_4[1], and_3_out, and_4_out);
  xor xor_3 (out_4[2], and_5_out, and_6_out);
  xor xor_4 (out_4[3], and_7_out, and_8_out);
  xor xor_5 (out_4[4], and_9_out, and_10_out);
  xor xor_6 (out_4[5], and_11_out, and_12_out);
  xor xor_7 (out_4[6], and_13_out, and_14_out);
  xor xor_8 (out_4[7], and_15_out, and_16_out);
  and and_17 (and_17_out, A[8], ~Controle);  // AND_Gate
  and and_18 (and_18_out, B[8], Controle);
  and and_19 (and_19_out, A[9], ~Controle);  // AND_Gate
  and and_20 (and_20_out, B[9], Controle);
  and and_21 (and_21_out, A[10], ~Controle);  // AND_Gate
  and and_22 (and_22_out, B[10], Controle);
  and and_23 (and_23_out, A[11], ~Controle);  // AND_Gate
  and and_24 (and_24_out, B[11], Controle);
  and and_25 (and_25_out, A[12], ~Controle);  // AND_Gate
  and and_26 (and_26_out, B[12], Controle);
  and and_27 (and_27_out, A[13], ~Controle);  // AND_Gate
  and and_28 (and_28_out, B[13], Controle);
  and and_29 (and_29_out, A[14], ~Controle);  // AND_Gate
  and and_30 (and_30_out, B[14], Controle);
  and and_31 (and_31_out, A[15], ~Controle);  // AND_Gate
  and and_32 (and_32_out, B[15], Controle);
  xor xor_9 (out_4[8], and_17_out, and_18_out);
  xor xor_10 (out_4[9], and_19_out, and_20_out);
  xor xor_11 (out_4[10], and_21_out, and_22_out);
  xor xor_12 (out_4[11], and_23_out, and_24_out);
  xor xor_13 (out_4[12], and_25_out, and_26_out);
  xor xor_14 (out_4[13], and_27_out, and_28_out);
  xor xor_15 (out_4[14], and_29_out, and_30_out);
  xor xor_16 (out_4[15], and_31_out, and_32_out);

  // Other names for the same wires on the sheet: s0 = out_4[0]; s1 = out_4[1]; s2 = out_4[2]; s3 = out_4[3];
  //   s4 = out_4[4]; s5 = out_4[5]; s6 = out_4[6]; s7 = out_4[7]; s8 = out_4[8]; s9 = out_4[9]; s10 = out_4[10];
  //   s11 = out_4[11]; s12 = out_4[12]; s13 = out_4[13]; s14 = out_4[14]; s15 = out_4[15]; SELECT = Controle

  // Notes on the sheet:
  //   na main mexendo com acc
  //   MUX 16x1
endmodule

module MUX_8x1 (
  input  [7:0] A,
  input  [7:0] B,
  input  control,
  output [7:0] out_4
);

  wire and_1_out, and_2_out, and_3_out, and_4_out, and_5_out, and_6_out, and_7_out, and_8_out, and_9_out,
       and_10_out, and_11_out, and_12_out, and_13_out, and_14_out, and_15_out, and_16_out;

  and and_1 (and_1_out, A[0], ~control);  // AND_Gate
  and and_2 (and_2_out, B[0], control);
  and and_3 (and_3_out, A[1], ~control);  // AND_Gate
  and and_4 (and_4_out, B[1], control);
  and and_5 (and_5_out, A[2], ~control);  // AND_Gate
  and and_6 (and_6_out, B[2], control);
  and and_7 (and_7_out, A[3], ~control);  // AND_Gate
  and and_8 (and_8_out, B[3], control);
  and and_9 (and_9_out, A[4], ~control);  // AND_Gate
  and and_10 (and_10_out, B[4], control);
  and and_11 (and_11_out, A[5], ~control);  // AND_Gate
  and and_12 (and_12_out, B[5], control);
  and and_13 (and_13_out, A[6], ~control);  // AND_Gate
  and and_14 (and_14_out, B[6], control);
  and and_15 (and_15_out, A[7], ~control);  // AND_Gate
  and and_16 (and_16_out, B[7], control);
  xor xor_1 (out_4[0], and_1_out, and_2_out);
  xor xor_2 (out_4[1], and_3_out, and_4_out);
  xor xor_3 (out_4[2], and_5_out, and_6_out);
  xor xor_4 (out_4[3], and_7_out, and_8_out);
  xor xor_5 (out_4[4], and_9_out, and_10_out);
  xor xor_6 (out_4[5], and_11_out, and_12_out);
  xor xor_7 (out_4[6], and_13_out, and_14_out);
  xor xor_8 (out_4[7], and_15_out, and_16_out);

  // Other names for the same wires on the sheet: s0 = out_4[0]; s1 = out_4[1]; s2 = out_4[2]; s3 = out_4[3];
  //   s4 = out_4[4]; s5 = out_4[5]; s6 = out_4[6]; s7 = out_4[7]; SELECT = control

  // Notes on the sheet:
  //   main mexendo com a RAM
  //   MUX 8x1
endmodule

// MUX
module MUX_3x5 (
  input  [2:0] A,
  input  [2:0] B,
  input  [2:0] C,
  input  [2:0] D,
  input  [2:0] E,
  input  [2:0] F,
  input  [2:0] G,
  input  [2:0] H,
  input  [2:0] I,
  input  [2:0] J,
  input  [2:0] K,
  input  [2:0] L,
  input  [2:0] M,
  input  [2:0] N,
  input  [2:0] O,
  input  [2:0] P,
  input  [2:0] Q,
  input  [2:0] R,
  input  [2:0] S,
  input  [2:0] T,
  input  [2:0] U,
  input  [2:0] V,
  input  [2:0] W,
  input  [2:0] X,
  input  [2:0] Y,
  input  [2:0] Z,
  input  [2:0] AA,
  input  [2:0] BB,
  input  [2:0] CC,
  input  [2:0] DD,
  input  [2:0] EE,
  input  [2:0] FF,
  input  [4:0] in_33,
  output [2:0] out_34
);

  wire d0_t, d1_t, d2_t, d3, d4, d5, d6, d7, d8, d9, d10, d11, d12, d13, d14, d15, d16, d17, d18, d19, d20,
       d21, d22, d23, d24, d25, d26, d27, d28, d29, d30, d31, dd0_t, dd1_t, dd2_t, dd3, dd4, dd5, dd6, dd7,
       dd8, dd9, dd10, dd11, dd12, dd13, dd14, dd15, dd16, dd17, dd18, dd19, dd20, dd21, dd22, dd23, dd24,
       dd25, dd26, dd27, dd28, dd29, dd30, dd31, ddd0, ddd1, ddd2, ddd3, ddd4, ddd5, ddd6, ddd7, ddd8, ddd9,
       ddd10, ddd11, ddd12, ddd13, ddd14, ddd15, ddd16, ddd17, ddd18, ddd19, ddd20, ddd21, ddd22, ddd23,
       ddd24, ddd25, ddd26, ddd27, ddd28, ddd29, ddd30, ddd31;

  and and_1 (d0_t, A[0], ~in_33[4], ~in_33[3], ~in_33[2], ~in_33[1], ~in_33[0]);  // AND_Gate
  and and_2 (d1_t, B[0], ~in_33[4], ~in_33[3], ~in_33[2], ~in_33[1], in_33[0]);  // AND_Gate
  and and_3 (d2_t, C[0], ~in_33[4], ~in_33[3], ~in_33[2], in_33[1], ~in_33[0]);  // AND_Gate
  and and_4 (d3, D[0], ~in_33[4], ~in_33[3], ~in_33[2], in_33[1], in_33[0]);  // AND_Gate
  and and_5 (d4, E[0], ~in_33[4], ~in_33[3], in_33[2], ~in_33[1], ~in_33[0]);  // AND_Gate
  and and_6 (d5, F[0], ~in_33[4], ~in_33[3], in_33[2], ~in_33[1], in_33[0]);  // AND_Gate
  and and_7 (d6, G[0], ~in_33[4], ~in_33[3], in_33[2], in_33[1], ~in_33[0]);  // AND_Gate
  and and_8 (d7, H[0], ~in_33[4], ~in_33[3], in_33[2], in_33[1], in_33[0]);  // AND_Gate
  and and_9 (d8, I[0], ~in_33[4], in_33[3], ~in_33[2], ~in_33[1], ~in_33[0]);  // AND_Gate
  and and_10 (d9, J[0], ~in_33[4], in_33[3], ~in_33[2], ~in_33[1], in_33[0]);  // AND_Gate
  and and_11 (d10, K[0], ~in_33[4], in_33[3], ~in_33[2], in_33[1], ~in_33[0]);  // AND_Gate
  and and_12 (d11, L[0], ~in_33[4], in_33[3], ~in_33[2], in_33[1], in_33[0]);  // AND_Gate
  and and_13 (d12, M[0], ~in_33[4], in_33[3], in_33[2], ~in_33[1], ~in_33[0]);  // AND_Gate
  and and_14 (d13, N[0], ~in_33[4], in_33[3], in_33[2], ~in_33[1], in_33[0]);  // AND_Gate
  and and_15 (d14, O[0], ~in_33[4], in_33[3], in_33[2], in_33[1], ~in_33[0]);  // AND_Gate
  and and_16 (d15, P[0], ~in_33[4], in_33[3], in_33[2], in_33[1], in_33[0]);  // AND_Gate
  and and_17 (d16, Q[0], in_33[4], ~in_33[3], ~in_33[2], ~in_33[1], ~in_33[0]);  // AND_Gate
  and and_18 (d17, R[0], in_33[4], ~in_33[3], ~in_33[2], ~in_33[1], in_33[0]);  // AND_Gate
  and and_19 (d18, S[0], in_33[4], ~in_33[3], ~in_33[2], in_33[1], ~in_33[0]);  // AND_Gate
  and and_20 (d19, T[0], in_33[4], ~in_33[3], ~in_33[2], in_33[1], in_33[0]);  // AND_Gate
  and and_21 (d20, U[0], in_33[4], ~in_33[3], in_33[2], ~in_33[1], ~in_33[0]);  // AND_Gate
  and and_22 (d21, V[0], in_33[4], ~in_33[3], in_33[2], ~in_33[1], in_33[0]);  // AND_Gate
  and and_23 (d22, W[0], in_33[4], ~in_33[3], in_33[2], in_33[1], ~in_33[0]);  // AND_Gate
  and and_24 (d23, X[0], in_33[4], ~in_33[3], in_33[2], in_33[1], in_33[0]);  // AND_Gate
  and and_25 (d24, Y[0], in_33[4], in_33[3], ~in_33[2], ~in_33[1], ~in_33[0]);  // AND_Gate
  and and_26 (d25, Z[0], in_33[4], in_33[3], ~in_33[2], ~in_33[1]);  // AND_Gate
  and and_27 (d26, AA[0], in_33[4], in_33[3], ~in_33[2], in_33[1], ~in_33[0]);  // AND_Gate
  and and_28 (d27, BB[0], in_33[4], in_33[3], ~in_33[2], in_33[1], in_33[0]);  // AND_Gate
  and and_29 (d28, CC[0], in_33[4], in_33[3], in_33[2], ~in_33[1], ~in_33[0]);  // AND_Gate
  and and_30 (d29, DD[0], in_33[4], in_33[3], in_33[2], ~in_33[1], in_33[0]);  // AND_Gate
  and and_31 (d30, EE[0], in_33[4], in_33[3], in_33[2], in_33[1], ~in_33[0]);  // AND_Gate
  and and_32 (d31, FF[0], in_33[4], in_33[3], in_33[2], in_33[1], in_33[0]);
  ExactlyOne xor_1 (
    .out(out_34[0]), .in0(d0_t), .in1(d1_t), .in2(d2_t), .in3(d3), .in4(d4), .in5(d5), .in6(d6), .in7(d7),
    .in8(d8), .in9(d9), .in10(d10), .in11(d11), .in12(d12), .in13(d13), .in14(d14), .in15(d15), .in16(d16),
    .in17(d17), .in18(d18), .in19(d19), .in20(d20), .in21(d21), .in22(d22), .in23(d23), .in24(d24),
    .in25(d25), .in26(d26), .in27(d27), .in28(d28), .in29(d29), .in30(d30), .in31(d31));
  and and_33 (dd0_t, A[1], ~in_33[4], ~in_33[3], ~in_33[2], ~in_33[1], ~in_33[0]);  // AND_Gate
  and and_34 (dd1_t, B[1], ~in_33[4], ~in_33[3], ~in_33[2], ~in_33[1], in_33[0]);  // AND_Gate
  and and_35 (dd2_t, C[1], ~in_33[4], ~in_33[3], ~in_33[2], in_33[1], ~in_33[0]);  // AND_Gate
  and and_36 (dd3, D[1], ~in_33[4], ~in_33[3], ~in_33[2], in_33[1], in_33[0]);  // AND_Gate
  and and_37 (dd4, E[1], ~in_33[4], ~in_33[3], in_33[2], ~in_33[1], ~in_33[0]);  // AND_Gate
  and and_38 (dd5, F[1], ~in_33[4], ~in_33[3], in_33[2], ~in_33[1], in_33[0]);  // AND_Gate
  and and_39 (dd6, G[1], ~in_33[4], ~in_33[3], in_33[2], in_33[1], ~in_33[0]);  // AND_Gate
  and and_40 (dd7, H[1], ~in_33[4], ~in_33[3], in_33[2], in_33[1], in_33[0]);  // AND_Gate
  and and_41 (dd8, I[1], ~in_33[4], in_33[3], ~in_33[2], ~in_33[1], ~in_33[0]);  // AND_Gate
  and and_42 (dd9, J[1], ~in_33[4], in_33[3], ~in_33[2], ~in_33[1], in_33[0]);  // AND_Gate
  and and_43 (dd10, K[1], ~in_33[4], in_33[3], ~in_33[2], in_33[1], ~in_33[0]);  // AND_Gate
  and and_44 (dd11, L[1], ~in_33[4], in_33[3], ~in_33[2], in_33[1], in_33[0]);  // AND_Gate
  and and_45 (dd12, M[1], ~in_33[4], in_33[3], in_33[2], ~in_33[1], ~in_33[0]);  // AND_Gate
  and and_46 (dd13, N[1], ~in_33[4], in_33[3], in_33[2], ~in_33[1], in_33[0]);  // AND_Gate
  and and_47 (dd14, O[1], ~in_33[4], in_33[3], in_33[2], in_33[1], ~in_33[0]);  // AND_Gate
  and and_48 (dd15, P[1], ~in_33[4], in_33[3], in_33[2], in_33[1], in_33[0]);  // AND_Gate
  and and_49 (dd16, Q[1], in_33[4], ~in_33[3], ~in_33[2], ~in_33[1], ~in_33[0]);  // AND_Gate
  and and_50 (dd17, R[1], in_33[4], ~in_33[3], ~in_33[2], ~in_33[1], in_33[0]);  // AND_Gate
  and and_51 (dd18, S[1], in_33[4], ~in_33[3], ~in_33[2], in_33[1], ~in_33[0]);  // AND_Gate
  and and_52 (dd19, T[1], in_33[4], ~in_33[3], ~in_33[2], in_33[1], in_33[0]);  // AND_Gate
  and and_53 (dd20, U[1], in_33[4], ~in_33[3], in_33[2], ~in_33[1], ~in_33[0]);  // AND_Gate
  and and_54 (dd21, V[1], in_33[4], ~in_33[3], in_33[2], ~in_33[1], in_33[0]);  // AND_Gate
  and and_55 (dd22, W[1], in_33[4], ~in_33[3], in_33[2], in_33[1], ~in_33[0]);  // AND_Gate
  and and_56 (dd23, X[1], in_33[4], ~in_33[3], in_33[2], in_33[1], in_33[0]);  // AND_Gate
  and and_57 (dd24, Y[1], in_33[4], in_33[3], ~in_33[2], ~in_33[1], ~in_33[0]);  // AND_Gate
  and and_58 (dd25, Z[1], in_33[4], in_33[3], ~in_33[2], ~in_33[1]);  // AND_Gate
  and and_59 (dd26, AA[1], in_33[4], in_33[3], ~in_33[2], in_33[1], ~in_33[0]);  // AND_Gate
  and and_60 (dd27, BB[1], in_33[4], in_33[3], ~in_33[2], in_33[1], in_33[0]);  // AND_Gate
  and and_61 (dd28, CC[1], in_33[4], in_33[3], in_33[2], ~in_33[1], ~in_33[0]);  // AND_Gate
  and and_62 (dd29, DD[1], in_33[4], in_33[3], in_33[2], ~in_33[1], in_33[0]);  // AND_Gate
  and and_63 (dd30, EE[1], in_33[4], in_33[3], in_33[2], in_33[1], ~in_33[0]);  // AND_Gate
  and and_64 (dd31, FF[1], in_33[4], in_33[3], in_33[2], in_33[1], in_33[0]);
  ExactlyOne xor_2 (
    .out(out_34[1]), .in0(dd0_t), .in1(dd1_t), .in2(dd2_t), .in3(dd3), .in4(dd4), .in5(dd5), .in6(dd6),
    .in7(dd7), .in8(dd8), .in9(dd9), .in10(dd10), .in11(dd11), .in12(dd12), .in13(dd13), .in14(dd14),
    .in15(dd15), .in16(dd16), .in17(dd17), .in18(dd18), .in19(dd19), .in20(dd20), .in21(dd21), .in22(dd22),
    .in23(dd23), .in24(dd24), .in25(dd25), .in26(dd26), .in27(dd27), .in28(dd28), .in29(dd29), .in30(dd30),
    .in31(dd31));
  and and_65 (ddd0, A[2], ~in_33[4], ~in_33[3], ~in_33[2], ~in_33[1], ~in_33[0]);  // AND_Gate
  and and_66 (ddd1, B[2], ~in_33[4], ~in_33[3], ~in_33[2], ~in_33[1], in_33[0]);  // AND_Gate
  and and_67 (ddd2, C[2], ~in_33[4], ~in_33[3], ~in_33[2], in_33[1], ~in_33[0]);  // AND_Gate
  and and_68 (ddd3, D[2], ~in_33[4], ~in_33[3], ~in_33[2], in_33[1], in_33[0]);  // AND_Gate
  and and_69 (ddd4, E[2], ~in_33[4], ~in_33[3], in_33[2], ~in_33[1], ~in_33[0]);  // AND_Gate
  and and_70 (ddd5, F[2], ~in_33[4], ~in_33[3], in_33[2], ~in_33[1], in_33[0]);  // AND_Gate
  and and_71 (ddd6, G[2], ~in_33[4], ~in_33[3], in_33[2], in_33[1], ~in_33[0]);  // AND_Gate
  and and_72 (ddd7, H[2], ~in_33[4], ~in_33[3], in_33[2], in_33[1], in_33[0]);  // AND_Gate
  and and_73 (ddd8, I[2], ~in_33[4], in_33[3], ~in_33[2], ~in_33[1], ~in_33[0]);  // AND_Gate
  and and_74 (ddd9, J[2], ~in_33[4], in_33[3], ~in_33[2], ~in_33[1], in_33[0]);  // AND_Gate
  and and_75 (ddd10, K[2], ~in_33[4], in_33[3], ~in_33[2], in_33[1], ~in_33[0]);  // AND_Gate
  and and_76 (ddd11, L[2], ~in_33[4], in_33[3], ~in_33[2], in_33[1], in_33[0]);  // AND_Gate
  and and_77 (ddd12, M[2], ~in_33[4], in_33[3], in_33[2], ~in_33[1], ~in_33[0]);  // AND_Gate
  and and_78 (ddd13, N[2], ~in_33[4], in_33[3], in_33[2], ~in_33[1], in_33[0]);  // AND_Gate
  and and_79 (ddd14, O[2], ~in_33[4], in_33[3], in_33[2], in_33[1], ~in_33[0]);  // AND_Gate
  and and_80 (ddd15, P[2], ~in_33[4], in_33[3], in_33[2], in_33[1], in_33[0]);  // AND_Gate
  and and_81 (ddd16, Q[2], in_33[4], ~in_33[3], ~in_33[2], ~in_33[1], ~in_33[0]);  // AND_Gate
  and and_82 (ddd17, R[2], in_33[4], ~in_33[3], ~in_33[2], ~in_33[1], in_33[0]);  // AND_Gate
  and and_83 (ddd18, S[2], in_33[4], ~in_33[3], ~in_33[2], in_33[1], ~in_33[0]);  // AND_Gate
  and and_84 (ddd19, T[2], in_33[4], ~in_33[3], ~in_33[2], in_33[1], in_33[0]);  // AND_Gate
  and and_85 (ddd20, U[2], in_33[4], ~in_33[3], in_33[2], ~in_33[1], ~in_33[0]);  // AND_Gate
  and and_86 (ddd21, V[2], in_33[4], ~in_33[3], in_33[2], ~in_33[1], in_33[0]);  // AND_Gate
  and and_87 (ddd22, W[2], in_33[4], ~in_33[3], in_33[2], in_33[1], ~in_33[0]);  // AND_Gate
  and and_88 (ddd23, X[2], in_33[4], ~in_33[3], in_33[2], in_33[1], in_33[0]);  // AND_Gate
  and and_89 (ddd24, Y[2], in_33[4], in_33[3], ~in_33[2], ~in_33[1], ~in_33[0]);  // AND_Gate
  and and_90 (ddd25, Z[2], in_33[4], in_33[3], ~in_33[2], ~in_33[1]);  // AND_Gate
  and and_91 (ddd26, AA[2], in_33[4], in_33[3], ~in_33[2], in_33[1], ~in_33[0]);  // AND_Gate
  and and_92 (ddd27, BB[2], in_33[4], in_33[3], ~in_33[2], in_33[1], in_33[0]);  // AND_Gate
  and and_93 (ddd28, CC[2], in_33[4], in_33[3], in_33[2], ~in_33[1], ~in_33[0]);  // AND_Gate
  and and_94 (ddd29, DD[2], in_33[4], in_33[3], in_33[2], ~in_33[1], in_33[0]);  // AND_Gate
  and and_95 (ddd30, EE[2], in_33[4], in_33[3], in_33[2], in_33[1], ~in_33[0]);  // AND_Gate
  and and_96 (ddd31, FF[2], in_33[4], in_33[3], in_33[2], in_33[1], in_33[0]);
  ExactlyOne xor_3 (
    .out(out_34[2]), .in0(ddd0), .in1(ddd1), .in2(ddd2), .in3(ddd3), .in4(ddd4), .in5(ddd5), .in6(ddd6),
    .in7(ddd7), .in8(ddd8), .in9(ddd9), .in10(ddd10), .in11(ddd11), .in12(ddd12), .in13(ddd13), .in14(ddd14),
    .in15(ddd15), .in16(ddd16), .in17(ddd17), .in18(ddd18), .in19(ddd19), .in20(ddd20), .in21(ddd21),
    .in22(ddd22), .in23(ddd23), .in24(ddd24), .in25(ddd25), .in26(ddd26), .in27(ddd27), .in28(ddd28),
    .in29(ddd29), .in30(ddd30), .in31(ddd31));

  // Other names for the same wires on the sheet: SELECT0 = in_33[0]; SELECT1 = in_33[1]; SELECT2 = in_33[2];
  //   SELECT3 = in_33[3]; SELECT4 = in_33[4]; SAIDA0 = out_34[0]; SAIDA1 = out_34[1]; SAIDA2 = out_34[2]

  // Notes on the sheet:
  //   control
endmodule

module MUX_1x3 (
  input  A,
  input  B,
  input  C,
  input  [2:0] control,
  input  D,
  input  E,
  input  F,
  input  G,
  input  H,
  output out_10
);

  wire and_1_out, and_2_out, and_3_out, and_4_out, and_5_out, and_6_out, and_7_out, and_8_out;

  and and_1 (and_1_out, A, ~control[2], ~control[1], ~control[0]);  // AND_Gate
  and and_2 (and_2_out, B, ~control[2], ~control[1], control[0]);  // AND_Gate
  and and_3 (and_3_out, C, ~control[2], control[1], ~control[0]);  // AND_Gate
  and and_4 (and_4_out, D, ~control[2], control[1], control[0]);  // AND_Gate
  and and_5 (and_5_out, E, control[2], ~control[1], ~control[0]);  // AND_Gate
  and and_6 (and_6_out, F, control[2], ~control[1], control[0]);  // AND_Gate
  and and_7 (and_7_out, G, control[2], control[1], ~control[0]);  // AND_Gate
  and and_8 (and_8_out, H, control[2], control[1], control[0]);
  ExactlyOne xor_1 (
    .out(out_10), .in0(and_1_out), .in1(and_2_out), .in2(and_3_out), .in3(and_4_out), .in4(and_5_out),
    .in5(and_6_out), .in6(and_7_out), .in7(and_8_out));

  // Other names for the same wires on the sheet: SELECT0 = control[0]; SELECT1 = control[1]; SELECT2 = control[2]

  // Notes on the sheet:
  //   MUX 1x3
  //   ULA overflow
endmodule

module MUX_16x3 (
  input  [15:0] A,
  input  [15:0] B,
  input  [15:0] C,
  input  [15:0] D,
  input  [15:0] E,
  input  [15:0] F,
  input  [15:0] G,
  input  [15:0] H,
  input  [2:0] in_9,
  output [15:0] out_10
);

  wire and_1_out, and_2_out, and_3_out, and_4_out, and_5_out, and_6_out, and_7_out, and_8_out, and_9_out,
       and_10_out, and_11_out, and_12_out, and_13_out, and_14_out, and_15_out, and_16_out, and_17_out,
       and_18_out, and_19_out, and_20_out, and_21_out, and_22_out, and_23_out, and_24_out, and_25_out,
       and_26_out, and_27_out, and_28_out, and_29_out, and_30_out, and_31_out, and_32_out, and_33_out,
       and_34_out, and_35_out, and_36_out, and_37_out, and_38_out, and_39_out, and_40_out, and_41_out,
       and_42_out, and_43_out, and_44_out, and_45_out, and_46_out, and_47_out, and_48_out, and_49_out,
       and_50_out, and_51_out, and_52_out, and_53_out, and_54_out, and_55_out, and_56_out, and_57_out,
       and_58_out, and_59_out, and_60_out, and_61_out, and_62_out, and_63_out, and_64_out, and_65_out,
       and_66_out, and_67_out, and_68_out, and_69_out, and_70_out, and_71_out, and_72_out, and_73_out,
       and_74_out, and_75_out, and_76_out, and_77_out, and_78_out, and_79_out, and_80_out, and_81_out,
       and_82_out, and_83_out, and_84_out, and_85_out, and_86_out, and_87_out, and_88_out, and_89_out,
       and_90_out, and_91_out, and_92_out, and_93_out, and_94_out, and_95_out, and_96_out, and_97_out,
       and_98_out, and_99_out, and_100_out, and_101_out, and_102_out, and_103_out, and_104_out, and_105_out,
       and_106_out, and_107_out, and_108_out, and_109_out, and_110_out, and_111_out, and_112_out,
       and_113_out, and_114_out, and_115_out, and_116_out, and_117_out, and_118_out, and_119_out,
       and_120_out, and_121_out, and_122_out, and_123_out, and_124_out, and_125_out, and_126_out,
       and_127_out, and_128_out;

  and and_1 (and_1_out, A[0], ~in_9[2], ~in_9[1], ~in_9[0]);  // AND_Gate
  and and_2 (and_2_out, B[0], ~in_9[2], ~in_9[1], in_9[0]);  // AND_Gate
  and and_3 (and_3_out, C[0], ~in_9[2], in_9[1], ~in_9[0]);  // AND_Gate
  and and_4 (and_4_out, D[0], ~in_9[2], in_9[1], in_9[0]);  // AND_Gate
  and and_5 (and_5_out, E[0], in_9[2], ~in_9[1], ~in_9[0]);  // AND_Gate
  and and_6 (and_6_out, F[0], in_9[2], ~in_9[1], in_9[0]);  // AND_Gate
  and and_7 (and_7_out, G[0], in_9[2], in_9[1], ~in_9[0]);  // AND_Gate
  and and_8 (and_8_out, H[0], in_9[2], in_9[1], in_9[0]);
  and and_9 (and_9_out, A[4], ~in_9[2], ~in_9[1], ~in_9[0]);  // AND_Gate
  and and_10 (and_10_out, B[4], ~in_9[2], ~in_9[1], in_9[0]);  // AND_Gate
  and and_11 (and_11_out, C[4], ~in_9[2], in_9[1], ~in_9[0]);  // AND_Gate
  and and_12 (and_12_out, D[4], ~in_9[2], in_9[1], in_9[0]);  // AND_Gate
  and and_13 (and_13_out, E[4], in_9[2], ~in_9[1], ~in_9[0]);  // AND_Gate
  and and_14 (and_14_out, F[4], in_9[2], ~in_9[1], in_9[0]);  // AND_Gate
  and and_15 (and_15_out, G[4], in_9[2], in_9[1], ~in_9[0]);  // AND_Gate
  and and_16 (and_16_out, H[4], in_9[2], in_9[1], in_9[0]);
  and and_17 (and_17_out, A[8], ~in_9[2], ~in_9[1], ~in_9[0]);  // AND_Gate
  and and_18 (and_18_out, B[8], ~in_9[2], ~in_9[1], in_9[0]);  // AND_Gate
  and and_19 (and_19_out, C[8], ~in_9[2], in_9[1], ~in_9[0]);  // AND_Gate
  and and_20 (and_20_out, D[8], ~in_9[2], in_9[1], in_9[0]);  // AND_Gate
  and and_21 (and_21_out, E[8], in_9[2], ~in_9[1], ~in_9[0]);  // AND_Gate
  and and_22 (and_22_out, F[8], in_9[2], ~in_9[1], in_9[0]);  // AND_Gate
  and and_23 (and_23_out, G[8], in_9[2], in_9[1], ~in_9[0]);  // AND_Gate
  and and_24 (and_24_out, H[8], in_9[2], in_9[1], in_9[0]);
  and and_25 (and_25_out, A[12], ~in_9[2], ~in_9[1], ~in_9[0]);  // AND_Gate
  and and_26 (and_26_out, B[12], ~in_9[2], ~in_9[1], in_9[0]);  // AND_Gate
  and and_27 (and_27_out, C[12], ~in_9[2], in_9[1], ~in_9[0]);  // AND_Gate
  and and_28 (and_28_out, D[12], ~in_9[2], in_9[1], in_9[0]);  // AND_Gate
  and and_29 (and_29_out, E[12], in_9[2], ~in_9[1], ~in_9[0]);  // AND_Gate
  and and_30 (and_30_out, F[12], in_9[2], ~in_9[1], in_9[0]);  // AND_Gate
  and and_31 (and_31_out, G[12], in_9[2], in_9[1], ~in_9[0]);  // AND_Gate
  and and_32 (and_32_out, H[12], in_9[2], in_9[1], in_9[0]);
  ExactlyOne xor_1 (
    .out(out_10[0]), .in0(and_1_out), .in1(and_2_out), .in2(and_3_out), .in3(and_4_out), .in4(and_5_out),
    .in5(and_6_out), .in6(and_7_out), .in7(and_8_out));
  ExactlyOne xor_2 (
    .out(out_10[4]), .in0(and_9_out), .in1(and_10_out), .in2(and_11_out), .in3(and_12_out), .in4(and_13_out),
    .in5(and_14_out), .in6(and_15_out), .in7(and_16_out));
  ExactlyOne xor_3 (
    .out(out_10[8]), .in0(and_17_out), .in1(and_18_out), .in2(and_19_out), .in3(and_20_out),
    .in4(and_21_out), .in5(and_22_out), .in6(and_23_out), .in7(and_24_out));
  ExactlyOne xor_4 (
    .out(out_10[12]), .in0(and_25_out), .in1(and_26_out), .in2(and_27_out), .in3(and_28_out),
    .in4(and_29_out), .in5(and_30_out), .in6(and_31_out), .in7(and_32_out));
  and and_33 (and_33_out, A[1], ~in_9[2], ~in_9[1], ~in_9[0]);  // AND_Gate
  and and_34 (and_34_out, B[1], ~in_9[2], ~in_9[1], in_9[0]);  // AND_Gate
  and and_35 (and_35_out, C[1], ~in_9[2], in_9[1], ~in_9[0]);  // AND_Gate
  and and_36 (and_36_out, D[1], ~in_9[2], in_9[1], in_9[0]);  // AND_Gate
  and and_37 (and_37_out, E[1], in_9[2], ~in_9[1], ~in_9[0]);  // AND_Gate
  and and_38 (and_38_out, F[1], in_9[2], ~in_9[1], in_9[0]);  // AND_Gate
  and and_39 (and_39_out, G[1], in_9[2], in_9[1], ~in_9[0]);  // AND_Gate
  and and_40 (and_40_out, H[1], in_9[2], in_9[1], in_9[0]);
  and and_41 (and_41_out, A[5], ~in_9[2], ~in_9[1], ~in_9[0]);  // AND_Gate
  and and_42 (and_42_out, B[5], ~in_9[2], ~in_9[1], in_9[0]);  // AND_Gate
  and and_43 (and_43_out, C[5], ~in_9[2], in_9[1], ~in_9[0]);  // AND_Gate
  and and_44 (and_44_out, D[5], ~in_9[2], in_9[1], in_9[0]);  // AND_Gate
  and and_45 (and_45_out, E[5], in_9[2], ~in_9[1], ~in_9[0]);  // AND_Gate
  and and_46 (and_46_out, F[5], in_9[2], ~in_9[1], in_9[0]);  // AND_Gate
  and and_47 (and_47_out, G[5], in_9[2], in_9[1], ~in_9[0]);  // AND_Gate
  and and_48 (and_48_out, H[5], in_9[2], in_9[1], in_9[0]);
  and and_49 (and_49_out, A[9], ~in_9[2], ~in_9[1], ~in_9[0]);  // AND_Gate
  and and_50 (and_50_out, B[9], ~in_9[2], ~in_9[1], in_9[0]);  // AND_Gate
  and and_51 (and_51_out, C[9], ~in_9[2], in_9[1], ~in_9[0]);  // AND_Gate
  and and_52 (and_52_out, D[9], ~in_9[2], in_9[1], in_9[0]);  // AND_Gate
  and and_53 (and_53_out, E[9], in_9[2], ~in_9[1], ~in_9[0]);  // AND_Gate
  and and_54 (and_54_out, F[9], in_9[2], ~in_9[1], in_9[0]);  // AND_Gate
  and and_55 (and_55_out, G[9], in_9[2], in_9[1], ~in_9[0]);  // AND_Gate
  and and_56 (and_56_out, H[9], in_9[2], in_9[1], in_9[0]);
  and and_57 (and_57_out, A[13], ~in_9[2], ~in_9[1], ~in_9[0]);  // AND_Gate
  and and_58 (and_58_out, B[13], ~in_9[2], ~in_9[1], in_9[0]);  // AND_Gate
  and and_59 (and_59_out, C[13], ~in_9[2], in_9[1], ~in_9[0]);  // AND_Gate
  and and_60 (and_60_out, D[13], ~in_9[2], in_9[1], in_9[0]);  // AND_Gate
  and and_61 (and_61_out, E[13], in_9[2], ~in_9[1], ~in_9[0]);  // AND_Gate
  and and_62 (and_62_out, F[13], in_9[2], ~in_9[1], in_9[0]);  // AND_Gate
  and and_63 (and_63_out, G[13], in_9[2], in_9[1], ~in_9[0]);  // AND_Gate
  and and_64 (and_64_out, H[13], in_9[2], in_9[1], in_9[0]);
  ExactlyOne xor_5 (
    .out(out_10[1]), .in0(and_33_out), .in1(and_34_out), .in2(and_35_out), .in3(and_36_out),
    .in4(and_37_out), .in5(and_38_out), .in6(and_39_out), .in7(and_40_out));
  ExactlyOne xor_6 (
    .out(out_10[5]), .in0(and_41_out), .in1(and_42_out), .in2(and_43_out), .in3(and_44_out),
    .in4(and_45_out), .in5(and_46_out), .in6(and_47_out), .in7(and_48_out));
  ExactlyOne xor_7 (
    .out(out_10[9]), .in0(and_49_out), .in1(and_50_out), .in2(and_51_out), .in3(and_52_out),
    .in4(and_53_out), .in5(and_54_out), .in6(and_55_out), .in7(and_56_out));
  ExactlyOne xor_8 (
    .out(out_10[13]), .in0(and_57_out), .in1(and_58_out), .in2(and_59_out), .in3(and_60_out),
    .in4(and_61_out), .in5(and_62_out), .in6(and_63_out), .in7(and_64_out));
  and and_65 (and_65_out, A[2], ~in_9[2], ~in_9[1], ~in_9[0]);  // AND_Gate
  and and_66 (and_66_out, B[2], ~in_9[2], ~in_9[1], in_9[0]);  // AND_Gate
  and and_67 (and_67_out, C[2], ~in_9[2], in_9[1], ~in_9[0]);  // AND_Gate
  and and_68 (and_68_out, D[2], ~in_9[2], in_9[1], in_9[0]);  // AND_Gate
  and and_69 (and_69_out, E[2], in_9[2], ~in_9[1], ~in_9[0]);  // AND_Gate
  and and_70 (and_70_out, F[2], in_9[2], ~in_9[1], in_9[0]);  // AND_Gate
  and and_71 (and_71_out, G[2], in_9[2], in_9[1], ~in_9[0]);  // AND_Gate
  and and_72 (and_72_out, H[2], in_9[2], in_9[1], in_9[0]);
  and and_73 (and_73_out, A[6], ~in_9[2], ~in_9[1], ~in_9[0]);  // AND_Gate
  and and_74 (and_74_out, B[6], ~in_9[2], ~in_9[1], in_9[0]);  // AND_Gate
  and and_75 (and_75_out, C[6], ~in_9[2], in_9[1], ~in_9[0]);  // AND_Gate
  and and_76 (and_76_out, D[6], ~in_9[2], in_9[1], in_9[0]);  // AND_Gate
  and and_77 (and_77_out, E[6], in_9[2], ~in_9[1], ~in_9[0]);  // AND_Gate
  and and_78 (and_78_out, F[6], in_9[2], ~in_9[1], in_9[0]);  // AND_Gate
  and and_79 (and_79_out, G[6], in_9[2], in_9[1], ~in_9[0]);  // AND_Gate
  and and_80 (and_80_out, H[6], in_9[2], in_9[1], in_9[0]);
  and and_81 (and_81_out, A[10], ~in_9[2], ~in_9[1], ~in_9[0]);  // AND_Gate
  and and_82 (and_82_out, B[10], ~in_9[2], ~in_9[1], in_9[0]);  // AND_Gate
  and and_83 (and_83_out, C[10], ~in_9[2], in_9[1], ~in_9[0]);  // AND_Gate
  and and_84 (and_84_out, D[10], ~in_9[2], in_9[1], in_9[0]);  // AND_Gate
  and and_85 (and_85_out, E[10], in_9[2], ~in_9[1], ~in_9[0]);  // AND_Gate
  and and_86 (and_86_out, F[10], in_9[2], ~in_9[1], in_9[0]);  // AND_Gate
  and and_87 (and_87_out, G[10], in_9[2], in_9[1], ~in_9[0]);  // AND_Gate
  and and_88 (and_88_out, H[10], in_9[2], in_9[1], in_9[0]);
  and and_89 (and_89_out, A[14], ~in_9[2], ~in_9[1], ~in_9[0]);  // AND_Gate
  and and_90 (and_90_out, B[14], ~in_9[2], ~in_9[1], in_9[0]);  // AND_Gate
  and and_91 (and_91_out, C[14], ~in_9[2], in_9[1], ~in_9[0]);  // AND_Gate
  and and_92 (and_92_out, D[14], ~in_9[2], in_9[1], in_9[0]);  // AND_Gate
  and and_93 (and_93_out, E[14], in_9[2], ~in_9[1], ~in_9[0]);  // AND_Gate
  and and_94 (and_94_out, F[14], in_9[2], ~in_9[1], in_9[0]);  // AND_Gate
  and and_95 (and_95_out, G[14], in_9[2], in_9[1], ~in_9[0]);  // AND_Gate
  and and_96 (and_96_out, H[14], in_9[2], in_9[1], in_9[0]);
  ExactlyOne xor_9 (
    .out(out_10[2]), .in0(and_65_out), .in1(and_66_out), .in2(and_67_out), .in3(and_68_out),
    .in4(and_69_out), .in5(and_70_out), .in6(and_71_out), .in7(and_72_out));
  ExactlyOne xor_10 (
    .out(out_10[6]), .in0(and_73_out), .in1(and_74_out), .in2(and_75_out), .in3(and_76_out),
    .in4(and_77_out), .in5(and_78_out), .in6(and_79_out), .in7(and_80_out));
  ExactlyOne xor_11 (
    .out(out_10[10]), .in0(and_81_out), .in1(and_82_out), .in2(and_83_out), .in3(and_84_out),
    .in4(and_85_out), .in5(and_86_out), .in6(and_87_out), .in7(and_88_out));
  ExactlyOne xor_12 (
    .out(out_10[14]), .in0(and_89_out), .in1(and_90_out), .in2(and_91_out), .in3(and_92_out),
    .in4(and_93_out), .in5(and_94_out), .in6(and_95_out), .in7(and_96_out));
  and and_97 (and_97_out, A[3], ~in_9[2], ~in_9[1], ~in_9[0]);  // AND_Gate
  and and_98 (and_98_out, B[3], ~in_9[2], ~in_9[1], in_9[0]);  // AND_Gate
  and and_99 (and_99_out, C[3], ~in_9[2], in_9[1], ~in_9[0]);  // AND_Gate
  and and_100 (and_100_out, D[3], ~in_9[2], in_9[1], in_9[0]);  // AND_Gate
  and and_101 (and_101_out, E[3], in_9[2], ~in_9[1], ~in_9[0]);  // AND_Gate
  and and_102 (and_102_out, F[3], in_9[2], ~in_9[1], in_9[0]);  // AND_Gate
  and and_103 (and_103_out, G[3], in_9[2], in_9[1], ~in_9[0]);  // AND_Gate
  and and_104 (and_104_out, H[3], in_9[2], in_9[1], in_9[0]);
  and and_105 (and_105_out, A[7], ~in_9[2], ~in_9[1], ~in_9[0]);  // AND_Gate
  and and_106 (and_106_out, B[7], ~in_9[2], ~in_9[1], in_9[0]);  // AND_Gate
  and and_107 (and_107_out, C[7], ~in_9[2], in_9[1], ~in_9[0]);  // AND_Gate
  and and_108 (and_108_out, D[7], ~in_9[2], in_9[1], in_9[0]);  // AND_Gate
  and and_109 (and_109_out, E[7], in_9[2], ~in_9[1], ~in_9[0]);  // AND_Gate
  and and_110 (and_110_out, F[7], in_9[2], ~in_9[1], in_9[0]);  // AND_Gate
  and and_111 (and_111_out, G[7], in_9[2], in_9[1], ~in_9[0]);  // AND_Gate
  and and_112 (and_112_out, H[7], in_9[2], in_9[1], in_9[0]);
  and and_113 (and_113_out, A[11], ~in_9[2], ~in_9[1], ~in_9[0]);  // AND_Gate
  and and_114 (and_114_out, B[11], ~in_9[2], ~in_9[1], in_9[0]);  // AND_Gate
  and and_115 (and_115_out, C[11], ~in_9[2], in_9[1], ~in_9[0]);  // AND_Gate
  and and_116 (and_116_out, D[11], ~in_9[2], in_9[1], in_9[0]);  // AND_Gate
  and and_117 (and_117_out, E[11], in_9[2], ~in_9[1], ~in_9[0]);  // AND_Gate
  and and_118 (and_118_out, F[11], in_9[2], ~in_9[1], in_9[0]);  // AND_Gate
  and and_119 (and_119_out, G[11], in_9[2], in_9[1], ~in_9[0]);  // AND_Gate
  and and_120 (and_120_out, H[11], in_9[2], in_9[1], in_9[0]);
  and and_121 (and_121_out, A[15], ~in_9[2], ~in_9[1], ~in_9[0]);  // AND_Gate
  and and_122 (and_122_out, B[15], ~in_9[2], ~in_9[1], in_9[0]);  // AND_Gate
  and and_123 (and_123_out, C[15], ~in_9[2], in_9[1], ~in_9[0]);  // AND_Gate
  and and_124 (and_124_out, D[15], ~in_9[2], in_9[1], in_9[0]);  // AND_Gate
  and and_125 (and_125_out, E[15], in_9[2], ~in_9[1], ~in_9[0]);  // AND_Gate
  and and_126 (and_126_out, F[15], in_9[2], ~in_9[1], in_9[0]);  // AND_Gate
  and and_127 (and_127_out, G[15], in_9[2], in_9[1], ~in_9[0]);  // AND_Gate
  and and_128 (and_128_out, H[15], in_9[2], in_9[1], in_9[0]);
  ExactlyOne xor_13 (
    .out(out_10[3]), .in0(and_97_out), .in1(and_98_out), .in2(and_99_out), .in3(and_100_out),
    .in4(and_101_out), .in5(and_102_out), .in6(and_103_out), .in7(and_104_out));
  ExactlyOne xor_14 (
    .out(out_10[7]), .in0(and_105_out), .in1(and_106_out), .in2(and_107_out), .in3(and_108_out),
    .in4(and_109_out), .in5(and_110_out), .in6(and_111_out), .in7(and_112_out));
  ExactlyOne xor_15 (
    .out(out_10[11]), .in0(and_113_out), .in1(and_114_out), .in2(and_115_out), .in3(and_116_out),
    .in4(and_117_out), .in5(and_118_out), .in6(and_119_out), .in7(and_120_out));
  ExactlyOne xor_16 (
    .out(out_10[15]), .in0(and_121_out), .in1(and_122_out), .in2(and_123_out), .in3(and_124_out),
    .in4(and_125_out), .in5(and_126_out), .in6(and_127_out), .in7(and_128_out));

  // Other names for the same wires on the sheet: SELECT0 = in_9[0]; SELECT1 = in_9[1]; SELECT2 = in_9[2];
  //   s0 = out_10[0]; s1 = out_10[1]; s2 = out_10[2]; s3 = out_10[3]; s4 = out_10[4]; s5 = out_10[5]; s6 = out_10[6];
  //   s7 = out_10[7]; s8 = out_10[8]; s9 = out_10[9]; s10 = out_10[10]; s11 = out_10[11]; s12 = out_10[12];
  //   s13 = out_10[13]; s14 = out_10[14]; s15 = out_10[15]

  // Notes on the sheet:
  //   ULA selecionando operação
  //   MUX 16x3
endmodule
