// Logisim project isPrime(4bits).circ as structural Verilog: 2 circuits, main circuit main
module main (
  input  [3:0] in_1,
  output out_2
);

  isPrime_4bits isprime_4bits_1 (.in1(in_1[0]), .in2(in_1[1]), .in3(in_1[2]), .in4(in_1[3]), .\output (out_2));
endmodule

module isPrime_4bits (
  input  in1,
  input  in2,
  input  in3,
  input  in4,
  output \output 
);

  wire and_1_out, and_2_out, and_3_out, and_4_out, not_1_out, not_2_out, not_3_out, not_4_out, not_5_out;

  not not_1 (not_1_out, in3);
  not not_2 (not_2_out, in4);
  not not_3 (not_3_out, in2);
  not not_4 (not_4_out, in3);
  not not_5 (not_5_out, in4);
  and and_1 (and_1_out, in1, in2, not_1_out);
  and and_2 (and_2_out, in1, in2, not_2_out);
  and and_3 (and_3_out, in1, not_3_out, in3);
  and and_4 (and_4_out, in2, not_4_out, not_5_out);
  or or_1 (\output , and_1_out, and_2_out, and_3_out, and_4_out);
endmodule
